// Logisim project Matrix Controller.circ as structural Verilog: 4 circuits, main circuit cell
module main (
  input  [4:0] adr,
  input  write,
  input  clock,
  input  [7:0] in_4,
  input  play
);

  wire decoder_1_out0, decoder_1_out1, decoder_1_out2, decoder_1_out3, decoder_1_out4, decoder_1_out5,
       decoder_1_out6, decoder_1_out7, decoder_1_out8, decoder_1_out9, decoder_1_out10, decoder_1_out11,
       decoder_1_out12, decoder_1_out13, decoder_1_out14, decoder_1_out15, newrow_1_out_62, newrow_1_out_63,
       newrow_1_out_64, newrow_1_out_65, newrow_1_out_66, newrow_1_out_67, newrow_1_out_68, newrow_1_out_69,
       newrow_1_out_70, newrow_1_out_71, newrow_1_out_72, newrow_1_out_73, newrow_1_out_74, newrow_1_out_75,
       newrow_1_out_76, newrow_1_out_77, newrow_2_clock_2, newrow_2_out_42, newrow_2_out_43, newrow_2_out_44,
       newrow_2_out_45, newrow_2_out_46, newrow_2_out_47, newrow_2_out_48, newrow_2_out_49, newrow_2_out_50,
       newrow_2_out_51, newrow_2_out_52, newrow_2_out_53, newrow_2_out_54, newrow_2_out_55, newrow_2_out_56,
       newrow_2_out_57, newrow_2_out_62, newrow_2_out_63, newrow_2_out_64, newrow_2_out_65, newrow_2_out_66,
       newrow_2_out_67, newrow_2_out_68, newrow_2_out_69, newrow_2_out_70, newrow_2_out_71, newrow_2_out_72,
       newrow_2_out_73, newrow_2_out_74, newrow_2_out_75, newrow_2_out_76, newrow_2_out_77, newrow_2_play_2,
       newrow_2_reset_2, newrow_3_clock_2, newrow_3_out_42, newrow_3_out_43, newrow_3_out_44,
       newrow_3_out_45, newrow_3_out_46, newrow_3_out_47, newrow_3_out_48, newrow_3_out_49, newrow_3_out_50,
       newrow_3_out_51, newrow_3_out_52, newrow_3_out_53, newrow_3_out_54, newrow_3_out_55, newrow_3_out_56,
       newrow_3_out_57, newrow_3_out_62, newrow_3_out_63, newrow_3_out_64, newrow_3_out_65, newrow_3_out_66,
       newrow_3_out_67, newrow_3_out_68, newrow_3_out_69, newrow_3_out_70, newrow_3_out_71, newrow_3_out_72,
       newrow_3_out_73, newrow_3_out_74, newrow_3_out_75, newrow_3_out_76, newrow_3_out_77, newrow_3_play_2,
       newrow_3_reset_2, newrow_4_clock_2, newrow_4_out_42, newrow_4_out_43, newrow_4_out_44,
       newrow_4_out_45, newrow_4_out_46, newrow_4_out_47, newrow_4_out_48, newrow_4_out_49, newrow_4_out_50,
       newrow_4_out_51, newrow_4_out_52, newrow_4_out_53, newrow_4_out_54, newrow_4_out_55, newrow_4_out_56,
       newrow_4_out_57, newrow_4_out_62, newrow_4_out_63, newrow_4_out_64, newrow_4_out_65, newrow_4_out_66,
       newrow_4_out_67, newrow_4_out_68, newrow_4_out_69, newrow_4_out_70, newrow_4_out_71, newrow_4_out_72,
       newrow_4_out_73, newrow_4_out_74, newrow_4_out_75, newrow_4_out_76, newrow_4_out_77, newrow_4_play_2,
       newrow_4_reset_2, newrow_5_clock_2, newrow_5_out_42, newrow_5_out_43, newrow_5_out_44,
       newrow_5_out_45, newrow_5_out_46, newrow_5_out_47, newrow_5_out_48, newrow_5_out_49, newrow_5_out_50,
       newrow_5_out_51, newrow_5_out_52, newrow_5_out_53, newrow_5_out_54, newrow_5_out_55, newrow_5_out_56,
       newrow_5_out_57, newrow_5_out_62, newrow_5_out_63, newrow_5_out_64, newrow_5_out_65, newrow_5_out_66,
       newrow_5_out_67, newrow_5_out_68, newrow_5_out_69, newrow_5_out_70, newrow_5_out_71, newrow_5_out_72,
       newrow_5_out_73, newrow_5_out_74, newrow_5_out_75, newrow_5_out_76, newrow_5_out_77, newrow_5_play_2,
       newrow_5_reset_2, newrow_6_clock_2, newrow_6_out_42, newrow_6_out_43, newrow_6_out_44,
       newrow_6_out_45, newrow_6_out_46, newrow_6_out_47, newrow_6_out_48, newrow_6_out_49, newrow_6_out_50,
       newrow_6_out_51, newrow_6_out_52, newrow_6_out_53, newrow_6_out_54, newrow_6_out_55, newrow_6_out_56,
       newrow_6_out_57, newrow_6_out_62, newrow_6_out_63, newrow_6_out_64, newrow_6_out_65, newrow_6_out_66,
       newrow_6_out_67, newrow_6_out_68, newrow_6_out_69, newrow_6_out_70, newrow_6_out_71, newrow_6_out_72,
       newrow_6_out_73, newrow_6_out_74, newrow_6_out_75, newrow_6_out_76, newrow_6_out_77, newrow_6_play_2,
       newrow_6_reset_2, newrow_7_clock_2, newrow_7_out_42, newrow_7_out_43, newrow_7_out_44,
       newrow_7_out_45, newrow_7_out_46, newrow_7_out_47, newrow_7_out_48, newrow_7_out_49, newrow_7_out_50,
       newrow_7_out_51, newrow_7_out_52, newrow_7_out_53, newrow_7_out_54, newrow_7_out_55, newrow_7_out_56,
       newrow_7_out_57, newrow_7_out_62, newrow_7_out_63, newrow_7_out_64, newrow_7_out_65, newrow_7_out_66,
       newrow_7_out_67, newrow_7_out_68, newrow_7_out_69, newrow_7_out_70, newrow_7_out_71, newrow_7_out_72,
       newrow_7_out_73, newrow_7_out_74, newrow_7_out_75, newrow_7_out_76, newrow_7_out_77, newrow_7_play_2,
       newrow_7_reset_2, newrow_8_clock_2, newrow_8_out_42, newrow_8_out_43, newrow_8_out_44,
       newrow_8_out_45, newrow_8_out_46, newrow_8_out_47, newrow_8_out_48, newrow_8_out_49, newrow_8_out_50,
       newrow_8_out_51, newrow_8_out_52, newrow_8_out_53, newrow_8_out_54, newrow_8_out_55, newrow_8_out_56,
       newrow_8_out_57, newrow_8_out_62, newrow_8_out_63, newrow_8_out_64, newrow_8_out_65, newrow_8_out_66,
       newrow_8_out_67, newrow_8_out_68, newrow_8_out_69, newrow_8_out_70, newrow_8_out_71, newrow_8_out_72,
       newrow_8_out_73, newrow_8_out_74, newrow_8_out_75, newrow_8_out_76, newrow_8_out_77, newrow_8_play_2,
       newrow_8_reset_2, newrow_9_clock_2, newrow_9_out_42, newrow_9_out_43, newrow_9_out_44,
       newrow_9_out_45, newrow_9_out_46, newrow_9_out_47, newrow_9_out_48, newrow_9_out_49, newrow_9_out_50,
       newrow_9_out_51, newrow_9_out_52, newrow_9_out_53, newrow_9_out_54, newrow_9_out_55, newrow_9_out_56,
       newrow_9_out_57, newrow_9_out_62, newrow_9_out_63, newrow_9_out_64, newrow_9_out_65, newrow_9_out_66,
       newrow_9_out_67, newrow_9_out_68, newrow_9_out_69, newrow_9_out_70, newrow_9_out_71, newrow_9_out_72,
       newrow_9_out_73, newrow_9_out_74, newrow_9_out_75, newrow_9_out_76, newrow_9_out_77, newrow_9_play_2,
       newrow_9_reset_2, newrow_10_clock_2, newrow_10_out_42, newrow_10_out_43, newrow_10_out_44,
       newrow_10_out_45, newrow_10_out_46, newrow_10_out_47, newrow_10_out_48, newrow_10_out_49,
       newrow_10_out_50, newrow_10_out_51, newrow_10_out_52, newrow_10_out_53, newrow_10_out_54,
       newrow_10_out_55, newrow_10_out_56, newrow_10_out_57, newrow_10_out_62, newrow_10_out_63,
       newrow_10_out_64, newrow_10_out_65, newrow_10_out_66, newrow_10_out_67, newrow_10_out_68,
       newrow_10_out_69, newrow_10_out_70, newrow_10_out_71, newrow_10_out_72, newrow_10_out_73,
       newrow_10_out_74, newrow_10_out_75, newrow_10_out_76, newrow_10_out_77, newrow_10_play_2,
       newrow_10_reset_2, newrow_11_clock_2, newrow_11_out_42, newrow_11_out_43, newrow_11_out_44,
       newrow_11_out_45, newrow_11_out_46, newrow_11_out_47, newrow_11_out_48, newrow_11_out_49,
       newrow_11_out_50, newrow_11_out_51, newrow_11_out_52, newrow_11_out_53, newrow_11_out_54,
       newrow_11_out_55, newrow_11_out_56, newrow_11_out_57, newrow_11_out_62, newrow_11_out_63,
       newrow_11_out_64, newrow_11_out_65, newrow_11_out_66, newrow_11_out_67, newrow_11_out_68,
       newrow_11_out_69, newrow_11_out_70, newrow_11_out_71, newrow_11_out_72, newrow_11_out_73,
       newrow_11_out_74, newrow_11_out_75, newrow_11_out_76, newrow_11_out_77, newrow_11_play_2,
       newrow_11_reset_2, newrow_12_clock_2, newrow_12_out_42, newrow_12_out_43, newrow_12_out_44,
       newrow_12_out_45, newrow_12_out_46, newrow_12_out_47, newrow_12_out_48, newrow_12_out_49,
       newrow_12_out_50, newrow_12_out_51, newrow_12_out_52, newrow_12_out_53, newrow_12_out_54,
       newrow_12_out_55, newrow_12_out_56, newrow_12_out_57, newrow_12_out_62, newrow_12_out_63,
       newrow_12_out_64, newrow_12_out_65, newrow_12_out_66, newrow_12_out_67, newrow_12_out_68,
       newrow_12_out_69, newrow_12_out_70, newrow_12_out_71, newrow_12_out_72, newrow_12_out_73,
       newrow_12_out_74, newrow_12_out_75, newrow_12_out_76, newrow_12_out_77, newrow_12_play_2,
       newrow_12_reset_2, newrow_13_clock_2, newrow_13_out_42, newrow_13_out_43, newrow_13_out_44,
       newrow_13_out_45, newrow_13_out_46, newrow_13_out_47, newrow_13_out_48, newrow_13_out_49,
       newrow_13_out_50, newrow_13_out_51, newrow_13_out_52, newrow_13_out_53, newrow_13_out_54,
       newrow_13_out_55, newrow_13_out_56, newrow_13_out_57, newrow_13_out_62, newrow_13_out_63,
       newrow_13_out_64, newrow_13_out_65, newrow_13_out_66, newrow_13_out_67, newrow_13_out_68,
       newrow_13_out_69, newrow_13_out_70, newrow_13_out_71, newrow_13_out_72, newrow_13_out_73,
       newrow_13_out_74, newrow_13_out_75, newrow_13_out_76, newrow_13_out_77, newrow_13_play_2,
       newrow_13_reset_2, newrow_14_clock_2, newrow_14_out_42, newrow_14_out_43, newrow_14_out_44,
       newrow_14_out_45, newrow_14_out_46, newrow_14_out_47, newrow_14_out_48, newrow_14_out_49,
       newrow_14_out_50, newrow_14_out_51, newrow_14_out_52, newrow_14_out_53, newrow_14_out_54,
       newrow_14_out_55, newrow_14_out_56, newrow_14_out_57, newrow_14_out_62, newrow_14_out_63,
       newrow_14_out_64, newrow_14_out_65, newrow_14_out_66, newrow_14_out_67, newrow_14_out_68,
       newrow_14_out_69, newrow_14_out_70, newrow_14_out_71, newrow_14_out_72, newrow_14_out_73,
       newrow_14_out_74, newrow_14_out_75, newrow_14_out_76, newrow_14_out_77, newrow_14_play_2,
       newrow_14_reset_2, newrow_15_clock_2, newrow_15_out_42, newrow_15_out_43, newrow_15_out_44,
       newrow_15_out_45, newrow_15_out_46, newrow_15_out_47, newrow_15_out_48, newrow_15_out_49,
       newrow_15_out_50, newrow_15_out_51, newrow_15_out_52, newrow_15_out_53, newrow_15_out_54,
       newrow_15_out_55, newrow_15_out_56, newrow_15_out_57, newrow_15_out_62, newrow_15_out_63,
       newrow_15_out_64, newrow_15_out_65, newrow_15_out_66, newrow_15_out_67, newrow_15_out_68,
       newrow_15_out_69, newrow_15_out_70, newrow_15_out_71, newrow_15_out_72, newrow_15_out_73,
       newrow_15_out_74, newrow_15_out_75, newrow_15_out_76, newrow_15_out_77, newrow_15_play_2,
       newrow_15_reset_2, newrow_16_clock_2, newrow_16_out_42, newrow_16_out_43, newrow_16_out_44,
       newrow_16_out_45, newrow_16_out_46, newrow_16_out_47, newrow_16_out_48, newrow_16_out_49,
       newrow_16_out_50, newrow_16_out_51, newrow_16_out_52, newrow_16_out_53, newrow_16_out_54,
       newrow_16_out_55, newrow_16_out_56, newrow_16_out_57, newrow_16_play_2, newrow_16_reset_2, reset_out;
  wire [3:0] newrow_2_die1_2, newrow_2_die2_2, newrow_2_resp_2, newrow_3_die1_2, newrow_3_die2_2,
       newrow_3_resp_2, newrow_4_die1_2, newrow_4_die2_2, newrow_4_resp_2, newrow_5_die1_2, newrow_5_die2_2,
       newrow_5_resp_2, newrow_6_die1_2, newrow_6_die2_2, newrow_6_resp_2, newrow_7_die1_2, newrow_7_die2_2,
       newrow_7_resp_2, newrow_8_die1_2, newrow_8_die2_2, newrow_8_resp_2, newrow_9_die1_2, newrow_9_die2_2,
       newrow_9_resp_2, newrow_10_die1_2, newrow_10_die2_2, newrow_10_resp_2, newrow_11_die1_2,
       newrow_11_die2_2, newrow_11_resp_2, newrow_12_die1_2, newrow_12_die2_2, newrow_12_resp_2,
       newrow_13_die1_2, newrow_13_die2_2, newrow_13_resp_2, newrow_14_die1_2, newrow_14_die2_2,
       newrow_14_resp_2, newrow_15_die1_2, newrow_15_die2_2, newrow_15_resp_2, newrow_16_die1_2,
       newrow_16_die2_2, newrow_16_resp_2;
  wire [15:0] newrow_1_out_80, newrow_2_out_80, newrow_3_out_80, newrow_4_out_80, newrow_5_out_80,
       newrow_6_out_80, newrow_7_out_80, newrow_8_out_80, newrow_9_out_80, newrow_10_out_80,
       newrow_11_out_80, newrow_12_out_80, newrow_13_out_80, newrow_14_out_80, newrow_15_out_80,
       newrow_16_out_80;

  Decoder #(.select(4), .disabled(0)) decoder_1 (
    .out0(decoder_1_out0), .out1(decoder_1_out1), .out2(decoder_1_out2), .out3(decoder_1_out3),
    .out4(decoder_1_out4), .out5(decoder_1_out5), .out6(decoder_1_out6), .out7(decoder_1_out7),
    .out8(decoder_1_out8), .out9(decoder_1_out9), .out10(decoder_1_out10), .out11(decoder_1_out11),
    .out12(decoder_1_out12), .out13(decoder_1_out13), .out14(decoder_1_out14), .out15(decoder_1_out15),
    .sel(adr[3:0]), .en(write));
  Button reset (.out(reset_out));
  newrow newrow_1 (
    .die1(newrow_2_die1_2), .die2(newrow_2_die2_2), .resp(newrow_2_resp_2), .clock(newrow_2_clock_2),
    .play(newrow_2_play_2), .data(in_4), .\byte (adr[4]), .write(decoder_1_out0), .out_80(newrow_1_out_80),
    .out_62(newrow_1_out_62), .in_23(newrow_2_out_42), .out_63(newrow_1_out_63), .in_24(newrow_2_out_43),
    .out_64(newrow_1_out_64), .in_25(newrow_2_out_44), .out_65(newrow_1_out_65), .in_26(newrow_2_out_45),
    .out_66(newrow_1_out_66), .in_27(newrow_2_out_46), .out_67(newrow_1_out_67), .in_28(newrow_2_out_47),
    .out_68(newrow_1_out_68), .in_29(newrow_2_out_48), .out_69(newrow_1_out_69), .in_30(newrow_2_out_49),
    .out_70(newrow_1_out_70), .in_31(newrow_2_out_50), .out_71(newrow_1_out_71), .in_32(newrow_2_out_51),
    .out_72(newrow_1_out_72), .in_33(newrow_2_out_52), .out_73(newrow_1_out_73), .in_34(newrow_2_out_53),
    .out_74(newrow_1_out_74), .in_35(newrow_2_out_54), .out_75(newrow_1_out_75), .in_36(newrow_2_out_55),
    .out_76(newrow_1_out_76), .in_37(newrow_2_out_56), .out_77(newrow_1_out_77), .in_38(newrow_2_out_57),
    .reset(newrow_2_reset_2));  // open: die1_2, die2_2, resp_2, clock_2, play_2, in_1, out_42, in_2, out_43, in_3, out_44, in_4, out_45, in_5, out_46, in_6, out_47, in_7, out_48, in_8, out_49, in_9, out_50, in_10, out_51, in_11, out_52, in_12, out_53, in_13, out_54, in_14, out_55, in_15, out_56, in_16, out_57, reset_2
  newrow newrow_2 (
    .die1(newrow_3_die1_2), .die2(newrow_3_die2_2), .resp(newrow_3_resp_2), .clock(newrow_3_clock_2),
    .play(newrow_3_play_2), .die1_2(newrow_2_die1_2), .die2_2(newrow_2_die2_2), .resp_2(newrow_2_resp_2),
    .clock_2(newrow_2_clock_2), .play_2(newrow_2_play_2), .data(in_4), .\byte (adr[4]),
    .write(decoder_1_out1), .out_80(newrow_2_out_80), .in_1(newrow_1_out_62), .out_42(newrow_2_out_42),
    .in_2(newrow_1_out_63), .out_43(newrow_2_out_43), .in_3(newrow_1_out_64), .out_44(newrow_2_out_44),
    .in_4(newrow_1_out_65), .out_45(newrow_2_out_45), .in_5(newrow_1_out_66), .out_46(newrow_2_out_46),
    .in_6(newrow_1_out_67), .out_47(newrow_2_out_47), .in_7(newrow_1_out_68), .out_48(newrow_2_out_48),
    .in_8(newrow_1_out_69), .out_49(newrow_2_out_49), .in_9(newrow_1_out_70), .out_50(newrow_2_out_50),
    .in_10(newrow_1_out_71), .out_51(newrow_2_out_51), .in_11(newrow_1_out_72), .out_52(newrow_2_out_52),
    .in_12(newrow_1_out_73), .out_53(newrow_2_out_53), .in_13(newrow_1_out_74), .out_54(newrow_2_out_54),
    .in_14(newrow_1_out_75), .out_55(newrow_2_out_55), .in_15(newrow_1_out_76), .out_56(newrow_2_out_56),
    .in_16(newrow_1_out_77), .out_57(newrow_2_out_57), .out_62(newrow_2_out_62), .in_23(newrow_3_out_42),
    .out_63(newrow_2_out_63), .in_24(newrow_3_out_43), .out_64(newrow_2_out_64), .in_25(newrow_3_out_44),
    .out_65(newrow_2_out_65), .in_26(newrow_3_out_45), .out_66(newrow_2_out_66), .in_27(newrow_3_out_46),
    .out_67(newrow_2_out_67), .in_28(newrow_3_out_47), .out_68(newrow_2_out_68), .in_29(newrow_3_out_48),
    .out_69(newrow_2_out_69), .in_30(newrow_3_out_49), .out_70(newrow_2_out_70), .in_31(newrow_3_out_50),
    .out_71(newrow_2_out_71), .in_32(newrow_3_out_51), .out_72(newrow_2_out_72), .in_33(newrow_3_out_52),
    .out_73(newrow_2_out_73), .in_34(newrow_3_out_53), .out_74(newrow_2_out_74), .in_35(newrow_3_out_54),
    .out_75(newrow_2_out_75), .in_36(newrow_3_out_55), .out_76(newrow_2_out_76), .in_37(newrow_3_out_56),
    .out_77(newrow_2_out_77), .in_38(newrow_3_out_57), .reset(newrow_3_reset_2), .reset_2(newrow_2_reset_2));
  newrow newrow_3 (
    .die1(newrow_4_die1_2), .die2(newrow_4_die2_2), .resp(newrow_4_resp_2), .clock(newrow_4_clock_2),
    .play(newrow_4_play_2), .die1_2(newrow_3_die1_2), .die2_2(newrow_3_die2_2), .resp_2(newrow_3_resp_2),
    .clock_2(newrow_3_clock_2), .play_2(newrow_3_play_2), .data(in_4), .\byte (adr[4]),
    .write(decoder_1_out2), .out_80(newrow_3_out_80), .in_1(newrow_2_out_62), .out_42(newrow_3_out_42),
    .in_2(newrow_2_out_63), .out_43(newrow_3_out_43), .in_3(newrow_2_out_64), .out_44(newrow_3_out_44),
    .in_4(newrow_2_out_65), .out_45(newrow_3_out_45), .in_5(newrow_2_out_66), .out_46(newrow_3_out_46),
    .in_6(newrow_2_out_67), .out_47(newrow_3_out_47), .in_7(newrow_2_out_68), .out_48(newrow_3_out_48),
    .in_8(newrow_2_out_69), .out_49(newrow_3_out_49), .in_9(newrow_2_out_70), .out_50(newrow_3_out_50),
    .in_10(newrow_2_out_71), .out_51(newrow_3_out_51), .in_11(newrow_2_out_72), .out_52(newrow_3_out_52),
    .in_12(newrow_2_out_73), .out_53(newrow_3_out_53), .in_13(newrow_2_out_74), .out_54(newrow_3_out_54),
    .in_14(newrow_2_out_75), .out_55(newrow_3_out_55), .in_15(newrow_2_out_76), .out_56(newrow_3_out_56),
    .in_16(newrow_2_out_77), .out_57(newrow_3_out_57), .out_62(newrow_3_out_62), .in_23(newrow_4_out_42),
    .out_63(newrow_3_out_63), .in_24(newrow_4_out_43), .out_64(newrow_3_out_64), .in_25(newrow_4_out_44),
    .out_65(newrow_3_out_65), .in_26(newrow_4_out_45), .out_66(newrow_3_out_66), .in_27(newrow_4_out_46),
    .out_67(newrow_3_out_67), .in_28(newrow_4_out_47), .out_68(newrow_3_out_68), .in_29(newrow_4_out_48),
    .out_69(newrow_3_out_69), .in_30(newrow_4_out_49), .out_70(newrow_3_out_70), .in_31(newrow_4_out_50),
    .out_71(newrow_3_out_71), .in_32(newrow_4_out_51), .out_72(newrow_3_out_72), .in_33(newrow_4_out_52),
    .out_73(newrow_3_out_73), .in_34(newrow_4_out_53), .out_74(newrow_3_out_74), .in_35(newrow_4_out_54),
    .out_75(newrow_3_out_75), .in_36(newrow_4_out_55), .out_76(newrow_3_out_76), .in_37(newrow_4_out_56),
    .out_77(newrow_3_out_77), .in_38(newrow_4_out_57), .reset(newrow_4_reset_2), .reset_2(newrow_3_reset_2));
  newrow newrow_4 (
    .die1(newrow_5_die1_2), .die2(newrow_5_die2_2), .resp(newrow_5_resp_2), .clock(newrow_5_clock_2),
    .play(newrow_5_play_2), .die1_2(newrow_4_die1_2), .die2_2(newrow_4_die2_2), .resp_2(newrow_4_resp_2),
    .clock_2(newrow_4_clock_2), .play_2(newrow_4_play_2), .data(in_4), .\byte (adr[4]),
    .write(decoder_1_out3), .out_80(newrow_4_out_80), .in_1(newrow_3_out_62), .out_42(newrow_4_out_42),
    .in_2(newrow_3_out_63), .out_43(newrow_4_out_43), .in_3(newrow_3_out_64), .out_44(newrow_4_out_44),
    .in_4(newrow_3_out_65), .out_45(newrow_4_out_45), .in_5(newrow_3_out_66), .out_46(newrow_4_out_46),
    .in_6(newrow_3_out_67), .out_47(newrow_4_out_47), .in_7(newrow_3_out_68), .out_48(newrow_4_out_48),
    .in_8(newrow_3_out_69), .out_49(newrow_4_out_49), .in_9(newrow_3_out_70), .out_50(newrow_4_out_50),
    .in_10(newrow_3_out_71), .out_51(newrow_4_out_51), .in_11(newrow_3_out_72), .out_52(newrow_4_out_52),
    .in_12(newrow_3_out_73), .out_53(newrow_4_out_53), .in_13(newrow_3_out_74), .out_54(newrow_4_out_54),
    .in_14(newrow_3_out_75), .out_55(newrow_4_out_55), .in_15(newrow_3_out_76), .out_56(newrow_4_out_56),
    .in_16(newrow_3_out_77), .out_57(newrow_4_out_57), .out_62(newrow_4_out_62), .in_23(newrow_5_out_42),
    .out_63(newrow_4_out_63), .in_24(newrow_5_out_43), .out_64(newrow_4_out_64), .in_25(newrow_5_out_44),
    .out_65(newrow_4_out_65), .in_26(newrow_5_out_45), .out_66(newrow_4_out_66), .in_27(newrow_5_out_46),
    .out_67(newrow_4_out_67), .in_28(newrow_5_out_47), .out_68(newrow_4_out_68), .in_29(newrow_5_out_48),
    .out_69(newrow_4_out_69), .in_30(newrow_5_out_49), .out_70(newrow_4_out_70), .in_31(newrow_5_out_50),
    .out_71(newrow_4_out_71), .in_32(newrow_5_out_51), .out_72(newrow_4_out_72), .in_33(newrow_5_out_52),
    .out_73(newrow_4_out_73), .in_34(newrow_5_out_53), .out_74(newrow_4_out_74), .in_35(newrow_5_out_54),
    .out_75(newrow_4_out_75), .in_36(newrow_5_out_55), .out_76(newrow_4_out_76), .in_37(newrow_5_out_56),
    .out_77(newrow_4_out_77), .in_38(newrow_5_out_57), .reset(newrow_5_reset_2), .reset_2(newrow_4_reset_2));
  newrow newrow_5 (
    .die1(newrow_6_die1_2), .die2(newrow_6_die2_2), .resp(newrow_6_resp_2), .clock(newrow_6_clock_2),
    .play(newrow_6_play_2), .die1_2(newrow_5_die1_2), .die2_2(newrow_5_die2_2), .resp_2(newrow_5_resp_2),
    .clock_2(newrow_5_clock_2), .play_2(newrow_5_play_2), .data(in_4), .\byte (adr[4]),
    .write(decoder_1_out4), .out_80(newrow_5_out_80), .in_1(newrow_4_out_62), .out_42(newrow_5_out_42),
    .in_2(newrow_4_out_63), .out_43(newrow_5_out_43), .in_3(newrow_4_out_64), .out_44(newrow_5_out_44),
    .in_4(newrow_4_out_65), .out_45(newrow_5_out_45), .in_5(newrow_4_out_66), .out_46(newrow_5_out_46),
    .in_6(newrow_4_out_67), .out_47(newrow_5_out_47), .in_7(newrow_4_out_68), .out_48(newrow_5_out_48),
    .in_8(newrow_4_out_69), .out_49(newrow_5_out_49), .in_9(newrow_4_out_70), .out_50(newrow_5_out_50),
    .in_10(newrow_4_out_71), .out_51(newrow_5_out_51), .in_11(newrow_4_out_72), .out_52(newrow_5_out_52),
    .in_12(newrow_4_out_73), .out_53(newrow_5_out_53), .in_13(newrow_4_out_74), .out_54(newrow_5_out_54),
    .in_14(newrow_4_out_75), .out_55(newrow_5_out_55), .in_15(newrow_4_out_76), .out_56(newrow_5_out_56),
    .in_16(newrow_4_out_77), .out_57(newrow_5_out_57), .out_62(newrow_5_out_62), .in_23(newrow_6_out_42),
    .out_63(newrow_5_out_63), .in_24(newrow_6_out_43), .out_64(newrow_5_out_64), .in_25(newrow_6_out_44),
    .out_65(newrow_5_out_65), .in_26(newrow_6_out_45), .out_66(newrow_5_out_66), .in_27(newrow_6_out_46),
    .out_67(newrow_5_out_67), .in_28(newrow_6_out_47), .out_68(newrow_5_out_68), .in_29(newrow_6_out_48),
    .out_69(newrow_5_out_69), .in_30(newrow_6_out_49), .out_70(newrow_5_out_70), .in_31(newrow_6_out_50),
    .out_71(newrow_5_out_71), .in_32(newrow_6_out_51), .out_72(newrow_5_out_72), .in_33(newrow_6_out_52),
    .out_73(newrow_5_out_73), .in_34(newrow_6_out_53), .out_74(newrow_5_out_74), .in_35(newrow_6_out_54),
    .out_75(newrow_5_out_75), .in_36(newrow_6_out_55), .out_76(newrow_5_out_76), .in_37(newrow_6_out_56),
    .out_77(newrow_5_out_77), .in_38(newrow_6_out_57), .reset(newrow_6_reset_2), .reset_2(newrow_5_reset_2));
  newrow newrow_6 (
    .die1(newrow_7_die1_2), .die2(newrow_7_die2_2), .resp(newrow_7_resp_2), .clock(newrow_7_clock_2),
    .play(newrow_7_play_2), .die1_2(newrow_6_die1_2), .die2_2(newrow_6_die2_2), .resp_2(newrow_6_resp_2),
    .clock_2(newrow_6_clock_2), .play_2(newrow_6_play_2), .data(in_4), .\byte (adr[4]),
    .write(decoder_1_out5), .out_80(newrow_6_out_80), .in_1(newrow_5_out_62), .out_42(newrow_6_out_42),
    .in_2(newrow_5_out_63), .out_43(newrow_6_out_43), .in_3(newrow_5_out_64), .out_44(newrow_6_out_44),
    .in_4(newrow_5_out_65), .out_45(newrow_6_out_45), .in_5(newrow_5_out_66), .out_46(newrow_6_out_46),
    .in_6(newrow_5_out_67), .out_47(newrow_6_out_47), .in_7(newrow_5_out_68), .out_48(newrow_6_out_48),
    .in_8(newrow_5_out_69), .out_49(newrow_6_out_49), .in_9(newrow_5_out_70), .out_50(newrow_6_out_50),
    .in_10(newrow_5_out_71), .out_51(newrow_6_out_51), .in_11(newrow_5_out_72), .out_52(newrow_6_out_52),
    .in_12(newrow_5_out_73), .out_53(newrow_6_out_53), .in_13(newrow_5_out_74), .out_54(newrow_6_out_54),
    .in_14(newrow_5_out_75), .out_55(newrow_6_out_55), .in_15(newrow_5_out_76), .out_56(newrow_6_out_56),
    .in_16(newrow_5_out_77), .out_57(newrow_6_out_57), .out_62(newrow_6_out_62), .in_23(newrow_7_out_42),
    .out_63(newrow_6_out_63), .in_24(newrow_7_out_43), .out_64(newrow_6_out_64), .in_25(newrow_7_out_44),
    .out_65(newrow_6_out_65), .in_26(newrow_7_out_45), .out_66(newrow_6_out_66), .in_27(newrow_7_out_46),
    .out_67(newrow_6_out_67), .in_28(newrow_7_out_47), .out_68(newrow_6_out_68), .in_29(newrow_7_out_48),
    .out_69(newrow_6_out_69), .in_30(newrow_7_out_49), .out_70(newrow_6_out_70), .in_31(newrow_7_out_50),
    .out_71(newrow_6_out_71), .in_32(newrow_7_out_51), .out_72(newrow_6_out_72), .in_33(newrow_7_out_52),
    .out_73(newrow_6_out_73), .in_34(newrow_7_out_53), .out_74(newrow_6_out_74), .in_35(newrow_7_out_54),
    .out_75(newrow_6_out_75), .in_36(newrow_7_out_55), .out_76(newrow_6_out_76), .in_37(newrow_7_out_56),
    .out_77(newrow_6_out_77), .in_38(newrow_7_out_57), .reset(newrow_7_reset_2), .reset_2(newrow_6_reset_2));
  newrow newrow_7 (
    .die1(newrow_8_die1_2), .die2(newrow_8_die2_2), .resp(newrow_8_resp_2), .clock(newrow_8_clock_2),
    .play(newrow_8_play_2), .die1_2(newrow_7_die1_2), .die2_2(newrow_7_die2_2), .resp_2(newrow_7_resp_2),
    .clock_2(newrow_7_clock_2), .play_2(newrow_7_play_2), .data(in_4), .\byte (adr[4]),
    .write(decoder_1_out6), .out_80(newrow_7_out_80), .in_1(newrow_6_out_62), .out_42(newrow_7_out_42),
    .in_2(newrow_6_out_63), .out_43(newrow_7_out_43), .in_3(newrow_6_out_64), .out_44(newrow_7_out_44),
    .in_4(newrow_6_out_65), .out_45(newrow_7_out_45), .in_5(newrow_6_out_66), .out_46(newrow_7_out_46),
    .in_6(newrow_6_out_67), .out_47(newrow_7_out_47), .in_7(newrow_6_out_68), .out_48(newrow_7_out_48),
    .in_8(newrow_6_out_69), .out_49(newrow_7_out_49), .in_9(newrow_6_out_70), .out_50(newrow_7_out_50),
    .in_10(newrow_6_out_71), .out_51(newrow_7_out_51), .in_11(newrow_6_out_72), .out_52(newrow_7_out_52),
    .in_12(newrow_6_out_73), .out_53(newrow_7_out_53), .in_13(newrow_6_out_74), .out_54(newrow_7_out_54),
    .in_14(newrow_6_out_75), .out_55(newrow_7_out_55), .in_15(newrow_6_out_76), .out_56(newrow_7_out_56),
    .in_16(newrow_6_out_77), .out_57(newrow_7_out_57), .out_62(newrow_7_out_62), .in_23(newrow_8_out_42),
    .out_63(newrow_7_out_63), .in_24(newrow_8_out_43), .out_64(newrow_7_out_64), .in_25(newrow_8_out_44),
    .out_65(newrow_7_out_65), .in_26(newrow_8_out_45), .out_66(newrow_7_out_66), .in_27(newrow_8_out_46),
    .out_67(newrow_7_out_67), .in_28(newrow_8_out_47), .out_68(newrow_7_out_68), .in_29(newrow_8_out_48),
    .out_69(newrow_7_out_69), .in_30(newrow_8_out_49), .out_70(newrow_7_out_70), .in_31(newrow_8_out_50),
    .out_71(newrow_7_out_71), .in_32(newrow_8_out_51), .out_72(newrow_7_out_72), .in_33(newrow_8_out_52),
    .out_73(newrow_7_out_73), .in_34(newrow_8_out_53), .out_74(newrow_7_out_74), .in_35(newrow_8_out_54),
    .out_75(newrow_7_out_75), .in_36(newrow_8_out_55), .out_76(newrow_7_out_76), .in_37(newrow_8_out_56),
    .out_77(newrow_7_out_77), .in_38(newrow_8_out_57), .reset(newrow_8_reset_2), .reset_2(newrow_7_reset_2));
  newrow newrow_8 (
    .die1(newrow_9_die1_2), .die2(newrow_9_die2_2), .resp(newrow_9_resp_2), .clock(newrow_9_clock_2),
    .play(newrow_9_play_2), .die1_2(newrow_8_die1_2), .die2_2(newrow_8_die2_2), .resp_2(newrow_8_resp_2),
    .clock_2(newrow_8_clock_2), .play_2(newrow_8_play_2), .data(in_4), .\byte (adr[4]),
    .write(decoder_1_out7), .out_80(newrow_8_out_80), .in_1(newrow_7_out_62), .out_42(newrow_8_out_42),
    .in_2(newrow_7_out_63), .out_43(newrow_8_out_43), .in_3(newrow_7_out_64), .out_44(newrow_8_out_44),
    .in_4(newrow_7_out_65), .out_45(newrow_8_out_45), .in_5(newrow_7_out_66), .out_46(newrow_8_out_46),
    .in_6(newrow_7_out_67), .out_47(newrow_8_out_47), .in_7(newrow_7_out_68), .out_48(newrow_8_out_48),
    .in_8(newrow_7_out_69), .out_49(newrow_8_out_49), .in_9(newrow_7_out_70), .out_50(newrow_8_out_50),
    .in_10(newrow_7_out_71), .out_51(newrow_8_out_51), .in_11(newrow_7_out_72), .out_52(newrow_8_out_52),
    .in_12(newrow_7_out_73), .out_53(newrow_8_out_53), .in_13(newrow_7_out_74), .out_54(newrow_8_out_54),
    .in_14(newrow_7_out_75), .out_55(newrow_8_out_55), .in_15(newrow_7_out_76), .out_56(newrow_8_out_56),
    .in_16(newrow_7_out_77), .out_57(newrow_8_out_57), .out_62(newrow_8_out_62), .in_23(newrow_9_out_42),
    .out_63(newrow_8_out_63), .in_24(newrow_9_out_43), .out_64(newrow_8_out_64), .in_25(newrow_9_out_44),
    .out_65(newrow_8_out_65), .in_26(newrow_9_out_45), .out_66(newrow_8_out_66), .in_27(newrow_9_out_46),
    .out_67(newrow_8_out_67), .in_28(newrow_9_out_47), .out_68(newrow_8_out_68), .in_29(newrow_9_out_48),
    .out_69(newrow_8_out_69), .in_30(newrow_9_out_49), .out_70(newrow_8_out_70), .in_31(newrow_9_out_50),
    .out_71(newrow_8_out_71), .in_32(newrow_9_out_51), .out_72(newrow_8_out_72), .in_33(newrow_9_out_52),
    .out_73(newrow_8_out_73), .in_34(newrow_9_out_53), .out_74(newrow_8_out_74), .in_35(newrow_9_out_54),
    .out_75(newrow_8_out_75), .in_36(newrow_9_out_55), .out_76(newrow_8_out_76), .in_37(newrow_9_out_56),
    .out_77(newrow_8_out_77), .in_38(newrow_9_out_57), .reset(newrow_9_reset_2), .reset_2(newrow_8_reset_2));
  newrow newrow_9 (
    .die1(newrow_10_die1_2), .die2(newrow_10_die2_2), .resp(newrow_10_resp_2), .clock(newrow_10_clock_2),
    .play(newrow_10_play_2), .die1_2(newrow_9_die1_2), .die2_2(newrow_9_die2_2), .resp_2(newrow_9_resp_2),
    .clock_2(newrow_9_clock_2), .play_2(newrow_9_play_2), .data(in_4), .\byte (adr[4]),
    .write(decoder_1_out8), .out_80(newrow_9_out_80), .in_1(newrow_8_out_62), .out_42(newrow_9_out_42),
    .in_2(newrow_8_out_63), .out_43(newrow_9_out_43), .in_3(newrow_8_out_64), .out_44(newrow_9_out_44),
    .in_4(newrow_8_out_65), .out_45(newrow_9_out_45), .in_5(newrow_8_out_66), .out_46(newrow_9_out_46),
    .in_6(newrow_8_out_67), .out_47(newrow_9_out_47), .in_7(newrow_8_out_68), .out_48(newrow_9_out_48),
    .in_8(newrow_8_out_69), .out_49(newrow_9_out_49), .in_9(newrow_8_out_70), .out_50(newrow_9_out_50),
    .in_10(newrow_8_out_71), .out_51(newrow_9_out_51), .in_11(newrow_8_out_72), .out_52(newrow_9_out_52),
    .in_12(newrow_8_out_73), .out_53(newrow_9_out_53), .in_13(newrow_8_out_74), .out_54(newrow_9_out_54),
    .in_14(newrow_8_out_75), .out_55(newrow_9_out_55), .in_15(newrow_8_out_76), .out_56(newrow_9_out_56),
    .in_16(newrow_8_out_77), .out_57(newrow_9_out_57), .out_62(newrow_9_out_62), .in_23(newrow_10_out_42),
    .out_63(newrow_9_out_63), .in_24(newrow_10_out_43), .out_64(newrow_9_out_64), .in_25(newrow_10_out_44),
    .out_65(newrow_9_out_65), .in_26(newrow_10_out_45), .out_66(newrow_9_out_66), .in_27(newrow_10_out_46),
    .out_67(newrow_9_out_67), .in_28(newrow_10_out_47), .out_68(newrow_9_out_68), .in_29(newrow_10_out_48),
    .out_69(newrow_9_out_69), .in_30(newrow_10_out_49), .out_70(newrow_9_out_70), .in_31(newrow_10_out_50),
    .out_71(newrow_9_out_71), .in_32(newrow_10_out_51), .out_72(newrow_9_out_72), .in_33(newrow_10_out_52),
    .out_73(newrow_9_out_73), .in_34(newrow_10_out_53), .out_74(newrow_9_out_74), .in_35(newrow_10_out_54),
    .out_75(newrow_9_out_75), .in_36(newrow_10_out_55), .out_76(newrow_9_out_76), .in_37(newrow_10_out_56),
    .out_77(newrow_9_out_77), .in_38(newrow_10_out_57), .reset(newrow_10_reset_2), .reset_2(newrow_9_reset_2));
  newrow newrow_10 (
    .die1(newrow_11_die1_2), .die2(newrow_11_die2_2), .resp(newrow_11_resp_2), .clock(newrow_11_clock_2),
    .play(newrow_11_play_2), .die1_2(newrow_10_die1_2), .die2_2(newrow_10_die2_2), .resp_2(newrow_10_resp_2),
    .clock_2(newrow_10_clock_2), .play_2(newrow_10_play_2), .data(in_4), .\byte (adr[4]),
    .write(decoder_1_out9), .out_80(newrow_10_out_80), .in_1(newrow_9_out_62), .out_42(newrow_10_out_42),
    .in_2(newrow_9_out_63), .out_43(newrow_10_out_43), .in_3(newrow_9_out_64), .out_44(newrow_10_out_44),
    .in_4(newrow_9_out_65), .out_45(newrow_10_out_45), .in_5(newrow_9_out_66), .out_46(newrow_10_out_46),
    .in_6(newrow_9_out_67), .out_47(newrow_10_out_47), .in_7(newrow_9_out_68), .out_48(newrow_10_out_48),
    .in_8(newrow_9_out_69), .out_49(newrow_10_out_49), .in_9(newrow_9_out_70), .out_50(newrow_10_out_50),
    .in_10(newrow_9_out_71), .out_51(newrow_10_out_51), .in_11(newrow_9_out_72), .out_52(newrow_10_out_52),
    .in_12(newrow_9_out_73), .out_53(newrow_10_out_53), .in_13(newrow_9_out_74), .out_54(newrow_10_out_54),
    .in_14(newrow_9_out_75), .out_55(newrow_10_out_55), .in_15(newrow_9_out_76), .out_56(newrow_10_out_56),
    .in_16(newrow_9_out_77), .out_57(newrow_10_out_57), .out_62(newrow_10_out_62), .in_23(newrow_11_out_42),
    .out_63(newrow_10_out_63), .in_24(newrow_11_out_43), .out_64(newrow_10_out_64), .in_25(newrow_11_out_44),
    .out_65(newrow_10_out_65), .in_26(newrow_11_out_45), .out_66(newrow_10_out_66), .in_27(newrow_11_out_46),
    .out_67(newrow_10_out_67), .in_28(newrow_11_out_47), .out_68(newrow_10_out_68), .in_29(newrow_11_out_48),
    .out_69(newrow_10_out_69), .in_30(newrow_11_out_49), .out_70(newrow_10_out_70), .in_31(newrow_11_out_50),
    .out_71(newrow_10_out_71), .in_32(newrow_11_out_51), .out_72(newrow_10_out_72), .in_33(newrow_11_out_52),
    .out_73(newrow_10_out_73), .in_34(newrow_11_out_53), .out_74(newrow_10_out_74), .in_35(newrow_11_out_54),
    .out_75(newrow_10_out_75), .in_36(newrow_11_out_55), .out_76(newrow_10_out_76), .in_37(newrow_11_out_56),
    .out_77(newrow_10_out_77), .in_38(newrow_11_out_57), .reset(newrow_11_reset_2),
    .reset_2(newrow_10_reset_2));
  newrow newrow_11 (
    .die1(newrow_12_die1_2), .die2(newrow_12_die2_2), .resp(newrow_12_resp_2), .clock(newrow_12_clock_2),
    .play(newrow_12_play_2), .die1_2(newrow_11_die1_2), .die2_2(newrow_11_die2_2), .resp_2(newrow_11_resp_2),
    .clock_2(newrow_11_clock_2), .play_2(newrow_11_play_2), .data(in_4), .\byte (adr[4]),
    .write(decoder_1_out10), .out_80(newrow_11_out_80), .in_1(newrow_10_out_62), .out_42(newrow_11_out_42),
    .in_2(newrow_10_out_63), .out_43(newrow_11_out_43), .in_3(newrow_10_out_64), .out_44(newrow_11_out_44),
    .in_4(newrow_10_out_65), .out_45(newrow_11_out_45), .in_5(newrow_10_out_66), .out_46(newrow_11_out_46),
    .in_6(newrow_10_out_67), .out_47(newrow_11_out_47), .in_7(newrow_10_out_68), .out_48(newrow_11_out_48),
    .in_8(newrow_10_out_69), .out_49(newrow_11_out_49), .in_9(newrow_10_out_70), .out_50(newrow_11_out_50),
    .in_10(newrow_10_out_71), .out_51(newrow_11_out_51), .in_11(newrow_10_out_72), .out_52(newrow_11_out_52),
    .in_12(newrow_10_out_73), .out_53(newrow_11_out_53), .in_13(newrow_10_out_74), .out_54(newrow_11_out_54),
    .in_14(newrow_10_out_75), .out_55(newrow_11_out_55), .in_15(newrow_10_out_76), .out_56(newrow_11_out_56),
    .in_16(newrow_10_out_77), .out_57(newrow_11_out_57), .out_62(newrow_11_out_62), .in_23(newrow_12_out_42),
    .out_63(newrow_11_out_63), .in_24(newrow_12_out_43), .out_64(newrow_11_out_64), .in_25(newrow_12_out_44),
    .out_65(newrow_11_out_65), .in_26(newrow_12_out_45), .out_66(newrow_11_out_66), .in_27(newrow_12_out_46),
    .out_67(newrow_11_out_67), .in_28(newrow_12_out_47), .out_68(newrow_11_out_68), .in_29(newrow_12_out_48),
    .out_69(newrow_11_out_69), .in_30(newrow_12_out_49), .out_70(newrow_11_out_70), .in_31(newrow_12_out_50),
    .out_71(newrow_11_out_71), .in_32(newrow_12_out_51), .out_72(newrow_11_out_72), .in_33(newrow_12_out_52),
    .out_73(newrow_11_out_73), .in_34(newrow_12_out_53), .out_74(newrow_11_out_74), .in_35(newrow_12_out_54),
    .out_75(newrow_11_out_75), .in_36(newrow_12_out_55), .out_76(newrow_11_out_76), .in_37(newrow_12_out_56),
    .out_77(newrow_11_out_77), .in_38(newrow_12_out_57), .reset(newrow_12_reset_2),
    .reset_2(newrow_11_reset_2));
  newrow newrow_12 (
    .die1(newrow_13_die1_2), .die2(newrow_13_die2_2), .resp(newrow_13_resp_2), .clock(newrow_13_clock_2),
    .play(newrow_13_play_2), .die1_2(newrow_12_die1_2), .die2_2(newrow_12_die2_2), .resp_2(newrow_12_resp_2),
    .clock_2(newrow_12_clock_2), .play_2(newrow_12_play_2), .data(in_4), .\byte (adr[4]),
    .write(decoder_1_out11), .out_80(newrow_12_out_80), .in_1(newrow_11_out_62), .out_42(newrow_12_out_42),
    .in_2(newrow_11_out_63), .out_43(newrow_12_out_43), .in_3(newrow_11_out_64), .out_44(newrow_12_out_44),
    .in_4(newrow_11_out_65), .out_45(newrow_12_out_45), .in_5(newrow_11_out_66), .out_46(newrow_12_out_46),
    .in_6(newrow_11_out_67), .out_47(newrow_12_out_47), .in_7(newrow_11_out_68), .out_48(newrow_12_out_48),
    .in_8(newrow_11_out_69), .out_49(newrow_12_out_49), .in_9(newrow_11_out_70), .out_50(newrow_12_out_50),
    .in_10(newrow_11_out_71), .out_51(newrow_12_out_51), .in_11(newrow_11_out_72), .out_52(newrow_12_out_52),
    .in_12(newrow_11_out_73), .out_53(newrow_12_out_53), .in_13(newrow_11_out_74), .out_54(newrow_12_out_54),
    .in_14(newrow_11_out_75), .out_55(newrow_12_out_55), .in_15(newrow_11_out_76), .out_56(newrow_12_out_56),
    .in_16(newrow_11_out_77), .out_57(newrow_12_out_57), .out_62(newrow_12_out_62), .in_23(newrow_13_out_42),
    .out_63(newrow_12_out_63), .in_24(newrow_13_out_43), .out_64(newrow_12_out_64), .in_25(newrow_13_out_44),
    .out_65(newrow_12_out_65), .in_26(newrow_13_out_45), .out_66(newrow_12_out_66), .in_27(newrow_13_out_46),
    .out_67(newrow_12_out_67), .in_28(newrow_13_out_47), .out_68(newrow_12_out_68), .in_29(newrow_13_out_48),
    .out_69(newrow_12_out_69), .in_30(newrow_13_out_49), .out_70(newrow_12_out_70), .in_31(newrow_13_out_50),
    .out_71(newrow_12_out_71), .in_32(newrow_13_out_51), .out_72(newrow_12_out_72), .in_33(newrow_13_out_52),
    .out_73(newrow_12_out_73), .in_34(newrow_13_out_53), .out_74(newrow_12_out_74), .in_35(newrow_13_out_54),
    .out_75(newrow_12_out_75), .in_36(newrow_13_out_55), .out_76(newrow_12_out_76), .in_37(newrow_13_out_56),
    .out_77(newrow_12_out_77), .in_38(newrow_13_out_57), .reset(newrow_13_reset_2),
    .reset_2(newrow_12_reset_2));
  newrow newrow_13 (
    .die1(newrow_14_die1_2), .die2(newrow_14_die2_2), .resp(newrow_14_resp_2), .clock(newrow_14_clock_2),
    .play(newrow_14_play_2), .die1_2(newrow_13_die1_2), .die2_2(newrow_13_die2_2), .resp_2(newrow_13_resp_2),
    .clock_2(newrow_13_clock_2), .play_2(newrow_13_play_2), .data(in_4), .\byte (adr[4]),
    .write(decoder_1_out12), .out_80(newrow_13_out_80), .in_1(newrow_12_out_62), .out_42(newrow_13_out_42),
    .in_2(newrow_12_out_63), .out_43(newrow_13_out_43), .in_3(newrow_12_out_64), .out_44(newrow_13_out_44),
    .in_4(newrow_12_out_65), .out_45(newrow_13_out_45), .in_5(newrow_12_out_66), .out_46(newrow_13_out_46),
    .in_6(newrow_12_out_67), .out_47(newrow_13_out_47), .in_7(newrow_12_out_68), .out_48(newrow_13_out_48),
    .in_8(newrow_12_out_69), .out_49(newrow_13_out_49), .in_9(newrow_12_out_70), .out_50(newrow_13_out_50),
    .in_10(newrow_12_out_71), .out_51(newrow_13_out_51), .in_11(newrow_12_out_72), .out_52(newrow_13_out_52),
    .in_12(newrow_12_out_73), .out_53(newrow_13_out_53), .in_13(newrow_12_out_74), .out_54(newrow_13_out_54),
    .in_14(newrow_12_out_75), .out_55(newrow_13_out_55), .in_15(newrow_12_out_76), .out_56(newrow_13_out_56),
    .in_16(newrow_12_out_77), .out_57(newrow_13_out_57), .out_62(newrow_13_out_62), .in_23(newrow_14_out_42),
    .out_63(newrow_13_out_63), .in_24(newrow_14_out_43), .out_64(newrow_13_out_64), .in_25(newrow_14_out_44),
    .out_65(newrow_13_out_65), .in_26(newrow_14_out_45), .out_66(newrow_13_out_66), .in_27(newrow_14_out_46),
    .out_67(newrow_13_out_67), .in_28(newrow_14_out_47), .out_68(newrow_13_out_68), .in_29(newrow_14_out_48),
    .out_69(newrow_13_out_69), .in_30(newrow_14_out_49), .out_70(newrow_13_out_70), .in_31(newrow_14_out_50),
    .out_71(newrow_13_out_71), .in_32(newrow_14_out_51), .out_72(newrow_13_out_72), .in_33(newrow_14_out_52),
    .out_73(newrow_13_out_73), .in_34(newrow_14_out_53), .out_74(newrow_13_out_74), .in_35(newrow_14_out_54),
    .out_75(newrow_13_out_75), .in_36(newrow_14_out_55), .out_76(newrow_13_out_76), .in_37(newrow_14_out_56),
    .out_77(newrow_13_out_77), .in_38(newrow_14_out_57), .reset(newrow_14_reset_2),
    .reset_2(newrow_13_reset_2));
  newrow newrow_14 (
    .die1(newrow_15_die1_2), .die2(newrow_15_die2_2), .resp(newrow_15_resp_2), .clock(newrow_15_clock_2),
    .play(newrow_15_play_2), .die1_2(newrow_14_die1_2), .die2_2(newrow_14_die2_2), .resp_2(newrow_14_resp_2),
    .clock_2(newrow_14_clock_2), .play_2(newrow_14_play_2), .data(in_4), .\byte (adr[4]),
    .write(decoder_1_out13), .out_80(newrow_14_out_80), .in_1(newrow_13_out_62), .out_42(newrow_14_out_42),
    .in_2(newrow_13_out_63), .out_43(newrow_14_out_43), .in_3(newrow_13_out_64), .out_44(newrow_14_out_44),
    .in_4(newrow_13_out_65), .out_45(newrow_14_out_45), .in_5(newrow_13_out_66), .out_46(newrow_14_out_46),
    .in_6(newrow_13_out_67), .out_47(newrow_14_out_47), .in_7(newrow_13_out_68), .out_48(newrow_14_out_48),
    .in_8(newrow_13_out_69), .out_49(newrow_14_out_49), .in_9(newrow_13_out_70), .out_50(newrow_14_out_50),
    .in_10(newrow_13_out_71), .out_51(newrow_14_out_51), .in_11(newrow_13_out_72), .out_52(newrow_14_out_52),
    .in_12(newrow_13_out_73), .out_53(newrow_14_out_53), .in_13(newrow_13_out_74), .out_54(newrow_14_out_54),
    .in_14(newrow_13_out_75), .out_55(newrow_14_out_55), .in_15(newrow_13_out_76), .out_56(newrow_14_out_56),
    .in_16(newrow_13_out_77), .out_57(newrow_14_out_57), .out_62(newrow_14_out_62), .in_23(newrow_15_out_42),
    .out_63(newrow_14_out_63), .in_24(newrow_15_out_43), .out_64(newrow_14_out_64), .in_25(newrow_15_out_44),
    .out_65(newrow_14_out_65), .in_26(newrow_15_out_45), .out_66(newrow_14_out_66), .in_27(newrow_15_out_46),
    .out_67(newrow_14_out_67), .in_28(newrow_15_out_47), .out_68(newrow_14_out_68), .in_29(newrow_15_out_48),
    .out_69(newrow_14_out_69), .in_30(newrow_15_out_49), .out_70(newrow_14_out_70), .in_31(newrow_15_out_50),
    .out_71(newrow_14_out_71), .in_32(newrow_15_out_51), .out_72(newrow_14_out_72), .in_33(newrow_15_out_52),
    .out_73(newrow_14_out_73), .in_34(newrow_15_out_53), .out_74(newrow_14_out_74), .in_35(newrow_15_out_54),
    .out_75(newrow_14_out_75), .in_36(newrow_15_out_55), .out_76(newrow_14_out_76), .in_37(newrow_15_out_56),
    .out_77(newrow_14_out_77), .in_38(newrow_15_out_57), .reset(newrow_15_reset_2),
    .reset_2(newrow_14_reset_2));
  newrow newrow_15 (
    .die1(newrow_16_die1_2), .die2(newrow_16_die2_2), .resp(newrow_16_resp_2), .clock(newrow_16_clock_2),
    .play(newrow_16_play_2), .die1_2(newrow_15_die1_2), .die2_2(newrow_15_die2_2), .resp_2(newrow_15_resp_2),
    .clock_2(newrow_15_clock_2), .play_2(newrow_15_play_2), .data(in_4), .\byte (adr[4]),
    .write(decoder_1_out14), .out_80(newrow_15_out_80), .in_1(newrow_14_out_62), .out_42(newrow_15_out_42),
    .in_2(newrow_14_out_63), .out_43(newrow_15_out_43), .in_3(newrow_14_out_64), .out_44(newrow_15_out_44),
    .in_4(newrow_14_out_65), .out_45(newrow_15_out_45), .in_5(newrow_14_out_66), .out_46(newrow_15_out_46),
    .in_6(newrow_14_out_67), .out_47(newrow_15_out_47), .in_7(newrow_14_out_68), .out_48(newrow_15_out_48),
    .in_8(newrow_14_out_69), .out_49(newrow_15_out_49), .in_9(newrow_14_out_70), .out_50(newrow_15_out_50),
    .in_10(newrow_14_out_71), .out_51(newrow_15_out_51), .in_11(newrow_14_out_72), .out_52(newrow_15_out_52),
    .in_12(newrow_14_out_73), .out_53(newrow_15_out_53), .in_13(newrow_14_out_74), .out_54(newrow_15_out_54),
    .in_14(newrow_14_out_75), .out_55(newrow_15_out_55), .in_15(newrow_14_out_76), .out_56(newrow_15_out_56),
    .in_16(newrow_14_out_77), .out_57(newrow_15_out_57), .out_62(newrow_15_out_62), .in_23(newrow_16_out_42),
    .out_63(newrow_15_out_63), .in_24(newrow_16_out_43), .out_64(newrow_15_out_64), .in_25(newrow_16_out_44),
    .out_65(newrow_15_out_65), .in_26(newrow_16_out_45), .out_66(newrow_15_out_66), .in_27(newrow_16_out_46),
    .out_67(newrow_15_out_67), .in_28(newrow_16_out_47), .out_68(newrow_15_out_68), .in_29(newrow_16_out_48),
    .out_69(newrow_15_out_69), .in_30(newrow_16_out_49), .out_70(newrow_15_out_70), .in_31(newrow_16_out_50),
    .out_71(newrow_15_out_71), .in_32(newrow_16_out_51), .out_72(newrow_15_out_72), .in_33(newrow_16_out_52),
    .out_73(newrow_15_out_73), .in_34(newrow_16_out_53), .out_74(newrow_15_out_74), .in_35(newrow_16_out_54),
    .out_75(newrow_15_out_75), .in_36(newrow_16_out_55), .out_76(newrow_15_out_76), .in_37(newrow_16_out_56),
    .out_77(newrow_15_out_77), .in_38(newrow_16_out_57), .reset(newrow_16_reset_2),
    .reset_2(newrow_15_reset_2));
  newrow newrow_16 (
    .die1(4'b0010), .die2(4'b0011), .resp(4'b0011), .clock(clock), .play(play), .die1_2(newrow_16_die1_2),
    .die2_2(newrow_16_die2_2), .resp_2(newrow_16_resp_2), .clock_2(newrow_16_clock_2),
    .play_2(newrow_16_play_2), .data(in_4), .\byte (adr[4]), .write(decoder_1_out15),
    .out_80(newrow_16_out_80), .in_1(newrow_15_out_62), .out_42(newrow_16_out_42), .in_2(newrow_15_out_63),
    .out_43(newrow_16_out_43), .in_3(newrow_15_out_64), .out_44(newrow_16_out_44), .in_4(newrow_15_out_65),
    .out_45(newrow_16_out_45), .in_5(newrow_15_out_66), .out_46(newrow_16_out_46), .in_6(newrow_15_out_67),
    .out_47(newrow_16_out_47), .in_7(newrow_15_out_68), .out_48(newrow_16_out_48), .in_8(newrow_15_out_69),
    .out_49(newrow_16_out_49), .in_9(newrow_15_out_70), .out_50(newrow_16_out_50), .in_10(newrow_15_out_71),
    .out_51(newrow_16_out_51), .in_11(newrow_15_out_72), .out_52(newrow_16_out_52), .in_12(newrow_15_out_73),
    .out_53(newrow_16_out_53), .in_13(newrow_15_out_74), .out_54(newrow_16_out_54), .in_14(newrow_15_out_75),
    .out_55(newrow_16_out_55), .in_15(newrow_15_out_76), .out_56(newrow_16_out_56), .in_16(newrow_15_out_77),
    .out_57(newrow_16_out_57), .reset(reset_out), .reset_2(newrow_16_reset_2));  // open: out_62, in_23, out_63, in_24, out_64, in_25, out_65, in_26, out_66, in_27, out_67, in_28, out_68, in_29, out_69, in_30, out_70, in_31, out_71, in_32, out_72, in_33, out_73, in_34, out_74, in_35, out_75, in_36, out_76, in_37, out_77, in_38
  DotMatrix #(.inputtype("row"), .matrixcols(16), .matrixrows(16)) dotmatrix_1 (
    .row0(newrow_1_out_80), .row1(newrow_2_out_80), .row2(newrow_3_out_80), .row3(newrow_4_out_80),
    .row4(newrow_5_out_80), .row5(newrow_6_out_80), .row6(newrow_7_out_80), .row7(newrow_8_out_80),
    .row8(newrow_9_out_80), .row9(newrow_10_out_80), .row10(newrow_11_out_80), .row11(newrow_12_out_80),
    .row12(newrow_13_out_80), .row13(newrow_14_out_80), .row14(newrow_15_out_80), .row15(newrow_16_out_80));
endmodule

module \cell  (
  input  [3:0] die1,
  input  [3:0] die2,
  input  [3:0] resp,
  input  in_4,
  input  in_5,
  input  in_6,
  input  in_7,
  input  in_8,
  input  in_9,
  input  in_10,
  input  in_11,
  input  write,
  input  play,
  input  clock,
  input  data,
  input  reset,
  output [3:0] out_17,
  output [3:0] out_18,
  output [3:0] out_19,
  output out_20,
  output out_21,
  output out_22,
  output out_23
);

  wire and_1_out, comparator_1_lt, comparator_2_gt, comparator_3_eq, multiplexer_1_out, multiplexer_2_out,
       or_1_out, or_2_out;
  wire [3:0] counter_1_out_9;

  counter counter_1 (
    .in_1(in_4), .in_2(in_5), .in_3(in_6), .in_4(in_7), .in_5(in_8), .in_6(in_9), .in_7(in_10), .in_8(in_11),
    .out_9(counter_1_out_9));
  Comparator #(.width(4), .mode("unsigned")) comparator_1 (
    .a(counter_1_out_9), .b(die1), .lt(comparator_1_lt));  // open: gt, eq
  or or_1 (or_1_out, comparator_1_lt, comparator_2_gt);
  Comparator #(.width(4), .mode("unsigned")) comparator_2 (
    .a(counter_1_out_9), .b(die2), .gt(comparator_2_gt));  // open: eq, lt
  or or_2 (or_2_out, out_20, comparator_3_eq);
  Comparator #(.width(4), .mode("unsigned")) comparator_3 (
    .a(counter_1_out_9), .b(resp), .eq(comparator_3_eq));  // open: gt, lt
  and and_1 (and_1_out, ~or_1_out, or_2_out);  // AND_Gate
  Multiplexer #(.enable("false")) multiplexer_1 (.in0(out_20), .in1(data), .out(multiplexer_1_out), .sel(write));
  Multiplexer #(.enable("false")) multiplexer_2 (
    .in0(multiplexer_1_out), .in1(and_1_out), .out(multiplexer_2_out), .sel(play));
  Register #(.width(1), .trigger("falling")) register_1 (
    .D(multiplexer_2_out), .Q(out_20), .clk(clock), .clr(reset));  // open: en

  assign out_17 = die1;
  assign out_18 = die2;
  assign out_19 = resp;
  assign out_21 = out_20;
  assign out_22 = out_20;
  assign out_23 = out_20;

  // Notes on the sheet:
  //   play - from counter
  //   !play + !write - state
  //   !play + write - data
endmodule

module counter (
  input  in_1,
  input  in_2,
  input  in_3,
  input  in_4,
  input  in_5,
  input  in_6,
  input  in_7,
  input  in_8,
  output [3:0] out_9
);

  wire [1:0] adder_1_out, adder_2_out, adder_3_out, adder_4_out, adder_5_out, adder_6_out;
  wire [2:2] adder_5_cout, adder_6_cout;

  Adder #(.width(1)) adder_1 (.a(in_1), .b(in_2), .out(adder_1_out[0]), .cout(adder_1_out[1]));  // open: cin
  Adder #(.width(1)) adder_2 (.a(in_3), .b(in_4), .out(adder_2_out[0]), .cout(adder_2_out[1]));  // open: cin
  Adder #(.width(1)) adder_3 (.a(in_5), .b(in_6), .out(adder_3_out[0]), .cout(adder_3_out[1]));  // open: cin
  Adder #(.width(1)) adder_4 (.a(in_7), .b(in_8), .out(adder_4_out[0]), .cout(adder_4_out[1]));  // open: cin
  Adder #(.width(2)) adder_5 (
    .a(adder_1_out), .b(adder_2_out), .out(adder_5_out), .cout(adder_5_cout[2]));  // open: cin
  Adder #(.width(2)) adder_6 (
    .a(adder_3_out), .b(adder_4_out), .out(adder_6_out), .cout(adder_6_cout[2]));  // open: cin
  Adder #(.width(3)) adder_7 (
    .a({adder_5_cout[2], adder_5_out}), .b({adder_6_cout[2], adder_6_out}), .out(out_9[2:0]), .cout(out_9[3]));  // open: cin
endmodule

module newrow (
  input  in_1,
  input  in_2,
  input  in_3,
  input  in_4,
  input  in_5,
  input  in_6,
  input  in_7,
  input  in_8,
  input  in_9,
  input  in_10,
  input  in_11,
  input  in_12,
  input  in_13,
  input  in_14,
  input  in_15,
  input  in_16,
  input  reset,
  input  [3:0] die1,
  input  [3:0] die2,
  input  [3:0] resp,
  input  clock,
  input  play,
  input  in_23,
  input  in_24,
  input  in_25,
  input  in_26,
  input  in_27,
  input  in_28,
  input  in_29,
  input  in_30,
  input  in_31,
  input  in_32,
  input  in_33,
  input  in_34,
  input  in_35,
  input  in_36,
  input  in_37,
  input  in_38,
  input  [7:0] data,
  input  \byte ,
  input  write,
  output out_42,
  output out_43,
  output out_44,
  output out_45,
  output out_46,
  output out_47,
  output out_48,
  output out_49,
  output out_50,
  output out_51,
  output out_52,
  output out_53,
  output out_54,
  output out_55,
  output out_56,
  output out_57,
  output reset_2,
  output [3:0] die1_2,
  output [3:0] die2_2,
  output [3:0] resp_2,
  output out_62,
  output out_63,
  output out_64,
  output out_65,
  output out_66,
  output out_67,
  output out_68,
  output out_69,
  output out_70,
  output out_71,
  output out_72,
  output out_73,
  output out_74,
  output out_75,
  output out_76,
  output out_77,
  output clock_2,
  output play_2,
  output [15:0] out_80
);

  wire cell_1_out_22, cell_2_out_21, cell_2_out_22, cell_3_out_21, cell_3_out_22, cell_4_out_21,
       cell_4_out_22, cell_5_out_21, cell_5_out_22, cell_6_out_21, cell_6_out_22, cell_7_out_21,
       cell_7_out_22, cell_8_out_21, cell_8_out_22, cell_9_out_21, cell_9_out_22, cell_10_out_21,
       cell_10_out_22, cell_11_out_21, cell_11_out_22, cell_12_out_21, cell_12_out_22, cell_13_out_21,
       cell_13_out_22, cell_14_out_21, cell_14_out_22, cell_15_out_21, cell_15_out_22, cell_16_out_21,
       decoder_1_out0, decoder_1_out1;
  wire [3:0] cell_1_out_17, cell_1_out_18, cell_1_out_19, cell_2_out_17, cell_2_out_18, cell_2_out_19,
       cell_3_out_17, cell_3_out_18, cell_3_out_19, cell_4_out_17, cell_4_out_18, cell_4_out_19,
       cell_5_out_17, cell_5_out_18, cell_5_out_19, cell_6_out_17, cell_6_out_18, cell_6_out_19,
       cell_7_out_17, cell_7_out_18, cell_7_out_19, cell_8_out_17, cell_8_out_18, cell_8_out_19,
       cell_9_out_17, cell_9_out_18, cell_9_out_19, cell_10_out_17, cell_10_out_18, cell_10_out_19,
       cell_11_out_17, cell_11_out_18, cell_11_out_19, cell_12_out_17, cell_12_out_18, cell_12_out_19,
       cell_13_out_17, cell_13_out_18, cell_13_out_19, cell_14_out_17, cell_14_out_18, cell_14_out_19,
       cell_15_out_17, cell_15_out_19;
  wire [7:0] demultiplexer_1_out0, demultiplexer_1_out1;

  Demultiplexer #(.width(8), .disabled(0), .enable("false")) demultiplexer_1 (
    .out0(demultiplexer_1_out0), .out1(demultiplexer_1_out1), .in(data), .sel(\byte ));
  Decoder #(.disabled(0)) decoder_1 (.out0(decoder_1_out0), .out1(decoder_1_out1), .sel(\byte ), .en(write));
  Pull_Resistor pull_resistor_1 (.node(in_1));
  \cell  cell_1 (
    .in_4(1'b0), .in_5(in_1), .in_6(in_2), .in_7(1'b0), .in_8(cell_2_out_21), .in_9(in_24), .in_10(1'b0),
    .in_11(in_23), .play(play), .clock(clock), .data(demultiplexer_1_out0[7]), .out_20(out_42),
    .out_22(cell_1_out_22), .out_23(out_62), .die2(die2), .resp(resp), .out_18(cell_1_out_18),
    .out_19(cell_1_out_19), .write(decoder_1_out0), .die1(die1), .out_17(cell_1_out_17), .reset(reset));  // open: out_21
  Pull_Resistor pull_resistor_2 (.node(in_23));
  Pull_Resistor pull_resistor_3 (.node(in_2));
  \cell  cell_2 (
    .in_4(in_1), .in_5(in_2), .in_6(in_3), .in_7(cell_1_out_22), .in_8(cell_3_out_21), .in_9(in_25),
    .in_10(in_23), .in_11(in_24), .play(play), .clock(clock), .data(demultiplexer_1_out0[6]),
    .out_20(out_43), .out_21(cell_2_out_21), .out_22(cell_2_out_22), .out_23(out_63), .die2(cell_1_out_18),
    .resp(cell_1_out_19), .out_18(cell_2_out_18), .out_19(cell_2_out_19), .write(decoder_1_out0),
    .die1(cell_1_out_17), .out_17(cell_2_out_17), .reset(reset));
  Pull_Resistor pull_resistor_4 (.node(in_24));
  Pull_Resistor pull_resistor_5 (.node(in_3));
  \cell  cell_3 (
    .in_4(in_2), .in_5(in_3), .in_6(in_4), .in_7(cell_2_out_22), .in_8(cell_4_out_21), .in_9(in_26),
    .in_10(in_24), .in_11(in_25), .play(play), .clock(clock), .data(demultiplexer_1_out0[5]),
    .out_20(out_44), .out_21(cell_3_out_21), .out_22(cell_3_out_22), .out_23(out_64), .die2(cell_2_out_18),
    .resp(cell_2_out_19), .out_18(cell_3_out_18), .out_19(cell_3_out_19), .write(decoder_1_out0),
    .die1(cell_2_out_17), .out_17(cell_3_out_17), .reset(reset));
  Pull_Resistor pull_resistor_6 (.node(in_25));
  Pull_Resistor pull_resistor_7 (.node(in_4));
  \cell  cell_4 (
    .in_4(in_3), .in_5(in_4), .in_6(in_5), .in_7(cell_3_out_22), .in_8(cell_5_out_21), .in_9(in_27),
    .in_10(in_25), .in_11(in_26), .play(play), .clock(clock), .data(demultiplexer_1_out0[4]),
    .out_20(out_45), .out_21(cell_4_out_21), .out_22(cell_4_out_22), .out_23(out_65), .die2(cell_3_out_18),
    .resp(cell_3_out_19), .out_18(cell_4_out_18), .out_19(cell_4_out_19), .write(decoder_1_out0),
    .die1(cell_3_out_17), .out_17(cell_4_out_17), .reset(reset));
  Pull_Resistor pull_resistor_8 (.node(in_26));
  Pull_Resistor pull_resistor_9 (.node(in_5));
  \cell  cell_5 (
    .in_4(in_4), .in_5(in_5), .in_6(in_6), .in_7(cell_4_out_22), .in_8(cell_6_out_21), .in_9(in_28),
    .in_10(in_26), .in_11(in_27), .play(play), .clock(clock), .data(demultiplexer_1_out0[3]),
    .out_20(out_46), .out_21(cell_5_out_21), .out_22(cell_5_out_22), .out_23(out_66), .die2(cell_4_out_18),
    .resp(cell_4_out_19), .out_18(cell_5_out_18), .out_19(cell_5_out_19), .write(decoder_1_out0),
    .die1(cell_4_out_17), .out_17(cell_5_out_17), .reset(reset));
  Pull_Resistor pull_resistor_10 (.node(in_27));
  Pull_Resistor pull_resistor_11 (.node(in_6));
  \cell  cell_6 (
    .in_4(in_5), .in_5(in_6), .in_6(in_7), .in_7(cell_5_out_22), .in_8(cell_7_out_21), .in_9(in_29),
    .in_10(in_27), .in_11(in_28), .play(play), .clock(clock), .data(demultiplexer_1_out0[2]),
    .out_20(out_47), .out_21(cell_6_out_21), .out_22(cell_6_out_22), .out_23(out_67), .die2(cell_5_out_18),
    .resp(cell_5_out_19), .out_18(cell_6_out_18), .out_19(cell_6_out_19), .write(decoder_1_out0),
    .die1(cell_5_out_17), .out_17(cell_6_out_17), .reset(reset));
  Pull_Resistor pull_resistor_12 (.node(in_28));
  Pull_Resistor pull_resistor_13 (.node(in_7));
  \cell  cell_7 (
    .in_4(in_6), .in_5(in_7), .in_6(in_8), .in_7(cell_6_out_22), .in_8(cell_8_out_21), .in_9(in_30),
    .in_10(in_28), .in_11(in_29), .play(play), .clock(clock), .data(demultiplexer_1_out0[1]),
    .out_20(out_48), .out_21(cell_7_out_21), .out_22(cell_7_out_22), .out_23(out_68), .die2(cell_6_out_18),
    .resp(cell_6_out_19), .out_18(cell_7_out_18), .out_19(cell_7_out_19), .write(decoder_1_out0),
    .die1(cell_6_out_17), .out_17(cell_7_out_17), .reset(reset));
  Pull_Resistor pull_resistor_14 (.node(in_29));
  Pull_Resistor pull_resistor_15 (.node(in_8));
  \cell  cell_8 (
    .in_4(in_7), .in_5(in_8), .in_6(in_9), .in_7(cell_7_out_22), .in_8(cell_9_out_21), .in_9(in_31),
    .in_10(in_29), .in_11(in_30), .play(play), .clock(clock), .data(demultiplexer_1_out0[0]),
    .out_20(out_49), .out_21(cell_8_out_21), .out_22(cell_8_out_22), .out_23(out_69), .die2(cell_7_out_18),
    .resp(cell_7_out_19), .out_18(cell_8_out_18), .out_19(cell_8_out_19), .write(decoder_1_out0),
    .die1(cell_7_out_17), .out_17(cell_8_out_17), .reset(reset));
  Pull_Resistor pull_resistor_16 (.node(in_30));
  Pull_Resistor pull_resistor_17 (.node(in_9));
  \cell  cell_9 (
    .in_4(in_8), .in_5(in_9), .in_6(in_10), .in_7(cell_8_out_22), .in_8(cell_10_out_21), .in_9(in_32),
    .in_10(in_30), .in_11(in_31), .play(play), .clock(clock), .data(demultiplexer_1_out1[7]),
    .out_20(out_50), .out_21(cell_9_out_21), .out_22(cell_9_out_22), .out_23(out_70), .die2(cell_8_out_18),
    .resp(cell_8_out_19), .out_18(cell_9_out_18), .out_19(cell_9_out_19), .write(decoder_1_out1),
    .die1(cell_8_out_17), .out_17(cell_9_out_17), .reset(reset));
  Pull_Resistor pull_resistor_18 (.node(in_31));
  Pull_Resistor pull_resistor_19 (.node(in_10));
  \cell  cell_10 (
    .in_4(in_9), .in_5(in_10), .in_6(in_11), .in_7(cell_9_out_22), .in_8(cell_11_out_21), .in_9(in_33),
    .in_10(in_31), .in_11(in_32), .play(play), .clock(clock), .data(demultiplexer_1_out1[6]),
    .out_20(out_51), .out_21(cell_10_out_21), .out_22(cell_10_out_22), .out_23(out_71), .die2(cell_9_out_18),
    .resp(cell_9_out_19), .out_18(cell_10_out_18), .out_19(cell_10_out_19), .write(decoder_1_out1),
    .die1(cell_9_out_17), .out_17(cell_10_out_17), .reset(reset));
  Pull_Resistor pull_resistor_20 (.node(in_32));
  Pull_Resistor pull_resistor_21 (.node(in_11));
  \cell  cell_11 (
    .in_4(in_10), .in_5(in_11), .in_6(in_12), .in_7(cell_10_out_22), .in_8(cell_12_out_21), .in_9(in_34),
    .in_10(in_32), .in_11(in_33), .play(play), .clock(clock), .data(demultiplexer_1_out1[5]),
    .out_20(out_52), .out_21(cell_11_out_21), .out_22(cell_11_out_22), .out_23(out_72),
    .die2(cell_10_out_18), .resp(cell_10_out_19), .out_18(cell_11_out_18), .out_19(cell_11_out_19),
    .write(decoder_1_out1), .die1(cell_10_out_17), .out_17(cell_11_out_17), .reset(reset));
  Pull_Resistor pull_resistor_22 (.node(in_33));
  Pull_Resistor pull_resistor_23 (.node(in_12));
  \cell  cell_12 (
    .in_4(in_11), .in_5(in_12), .in_6(in_13), .in_7(cell_11_out_22), .in_8(cell_13_out_21), .in_9(in_35),
    .in_10(in_33), .in_11(in_34), .play(play), .clock(clock), .data(demultiplexer_1_out1[4]),
    .out_20(out_53), .out_21(cell_12_out_21), .out_22(cell_12_out_22), .out_23(out_73),
    .die2(cell_11_out_18), .resp(cell_11_out_19), .out_18(cell_12_out_18), .out_19(cell_12_out_19),
    .write(decoder_1_out1), .die1(cell_11_out_17), .out_17(cell_12_out_17), .reset(reset));
  Pull_Resistor pull_resistor_24 (.node(in_34));
  Pull_Resistor pull_resistor_25 (.node(in_13));
  \cell  cell_13 (
    .in_4(in_12), .in_5(in_13), .in_6(in_14), .in_7(cell_12_out_22), .in_8(cell_14_out_21), .in_9(in_36),
    .in_10(in_34), .in_11(in_35), .play(play), .clock(clock), .data(demultiplexer_1_out1[3]),
    .out_20(out_54), .out_21(cell_13_out_21), .out_22(cell_13_out_22), .out_23(out_74),
    .die2(cell_12_out_18), .resp(cell_12_out_19), .out_18(cell_13_out_18), .out_19(cell_13_out_19),
    .write(decoder_1_out1), .die1(cell_12_out_17), .out_17(cell_13_out_17), .reset(reset));
  Pull_Resistor pull_resistor_26 (.node(in_35));
  Pull_Resistor pull_resistor_27 (.node(in_14));
  \cell  cell_14 (
    .in_4(in_13), .in_5(in_14), .in_6(in_15), .in_7(cell_13_out_22), .in_8(cell_15_out_21), .in_9(in_37),
    .in_10(in_35), .in_11(in_36), .play(play), .clock(clock), .data(demultiplexer_1_out1[2]),
    .out_20(out_55), .out_21(cell_14_out_21), .out_22(cell_14_out_22), .out_23(out_75),
    .die2(cell_13_out_18), .resp(cell_13_out_19), .out_18(cell_14_out_18), .out_19(cell_14_out_19),
    .write(decoder_1_out1), .die1(cell_13_out_17), .out_17(cell_14_out_17), .reset(reset));
  Pull_Resistor pull_resistor_28 (.node(in_36));
  Pull_Resistor pull_resistor_29 (.node(in_15));
  \cell  cell_15 (
    .in_4(in_14), .in_5(in_15), .in_6(in_16), .in_7(cell_14_out_22), .in_8(cell_16_out_21), .in_9(in_38),
    .in_10(in_36), .in_11(in_37), .play(play), .clock(clock), .data(demultiplexer_1_out1[1]),
    .out_20(out_56), .out_21(cell_15_out_21), .out_22(cell_15_out_22), .out_23(out_76),
    .die2(cell_14_out_18), .resp(cell_14_out_19), .out_19(cell_15_out_19), .write(decoder_1_out1),
    .die1(cell_14_out_17), .out_17(cell_15_out_17), .reset(reset));  // open: out_18
  Pull_Resistor pull_resistor_30 (.node(in_37));
  Pull_Resistor pull_resistor_31 (.node(in_16));
  \cell  cell_16 (
    .in_4(in_15), .in_5(in_16), .in_6(1'b0), .in_7(cell_15_out_22), .in_8(1'b0), .in_9(1'b0), .in_10(in_37),
    .in_11(in_38), .play(play), .clock(clock), .data(demultiplexer_1_out1[0]), .out_20(out_57),
    .out_21(cell_16_out_21), .out_23(out_77), .resp(cell_15_out_19), .write(decoder_1_out1),
    .die1(cell_15_out_17), .reset(reset));  // open: out_22, die2, out_18, out_19, out_17
  Pull_Resistor pull_resistor_32 (.node(in_38));

  assign clock_2 = clock;
  assign die1_2 = die1;
  assign die2_2 = die2;
  assign out_80 = {out_62, out_63, out_64, out_65, out_66, out_67, out_68, out_69, out_70, out_71, out_72, out_73, out_74, out_75, out_76, out_77};
  assign play_2 = play;
  assign reset_2 = reset;
  assign resp_2 = resp;
endmodule
