// Logisim project IntArbiter.circ as structural Verilog: 1 circuit, main circuit main
module main (
  input  [5:0] vecbus,
  input  IRQ,
  input  Rset,
  input  clock,
  input  IAck,
  input  [5:0] vec,
  input  IRQ_2,
  input  [1:0] status,
  output IRQ_3,
  output IAck_2,
  output IAck_3
);

  wire and_1_out, and_2_out, and_3_out, decoder_1_out0, decoder_1_out1, FE_out, nand_1_out, nor_1_out,
       not_1_out, not_2_out, not_3_out, not_4_out, not_5_out, not_6_out, not_7_out, or_2_out, or_3_out,
       or_4_out, RE_out, S0_out, S1_out, S2_out, s_r_ff_1_qn;
  wire [1:0] counter_1_q;

  or or_1 (IRQ_3, or_3_out, IAck_3);
  Counter #(.width(2), .max('h2)) counter_1 (
    .Q(counter_1_q), .clk(or_2_out), .clr(Rset));  // open: load, D, count, carry
  nand nand_1 (nand_1_out, status[0], ~status[1]);  // NAND_Gate
  Decoder #(.select(2), .enable("false")) decoder_1 (
    .out0(decoder_1_out0), .out1(decoder_1_out1), .out2(IAck_3), .sel(counter_1_q));  // open: out3
  and and_1 (and_1_out, IAck, nand_1_out);
  assign vecbus = IAck_3 ? vec : 6'bz;  // Controlled_Buffer controlled_buffer_1
  or or_2 (or_2_out, S2_out, S1_out, S0_out);
  or or_3 (or_3_out, and_2_out, decoder_1_out1);
  and S2 (S2_out, IAck_3, ~and_1_out);  // AND_Gate
  and and_2 (and_2_out, IRQ, not_1_out);
  and S1 (S1_out, decoder_1_out1, and_1_out);
  and S0 (S0_out, decoder_1_out0, s_r_ff_1_qn, not_3_out);
  not not_1 (not_1_out, not_2_out);
  not not_2 (not_2_out, decoder_1_out0);
  not not_3 (not_3_out, not_4_out);
  not not_4 (not_4_out, IRQ_2);
  not not_5 (not_5_out, clock);
  and and_3 (and_3_out, not_5_out, clock);
  nor nor_1 (nor_1_out, clock, not_6_out);
  not not_6 (not_6_out, clock);
  and RE (RE_out, ~IRQ_2, and_1_out, not_7_out);  // AND_Gate
  not not_7 (not_7_out, and_1_out);
  nor FE (FE_out, not_7_out, and_1_out);
  or or_4 (or_4_out, Rset, FE_out);
  S_R_Flip_Flop #(.trigger("high")) s_r_ff_1 (
    .S(RE_out), .clk(1'b1), .R(or_4_out), .Q(IAck_2), .Qn(s_r_ff_1_qn));  // open: preset, reset, en

  // Notes on the sheet:
  //   idle
  //   disable
  //   IAck
endmodule
