// Logisim project Matrix_Controller.circ as structural Verilog: 8 circuits, main circuit main
module main (
  input  in_out_prime,
  input  [7:0] I_Oaddr,
  input  I_Osel,
  input  [15:0] I_Odat,
  input  clock,
  input  reset,
  output [15:0] I_Odat_2,
  output [31:0] out_8,
  output [31:0] out_9,
  output [31:0] out_10,
  output [31:0] out_11,
  output [31:0] out_12,
  output [31:0] out_13,
  output [31:0] out_14,
  output [31:0] out_15,
  output [31:0] out_16,
  output [31:0] out_17,
  output [31:0] out_18,
  output [31:0] out_19,
  output [31:0] out_20,
  output [31:0] out_21,
  output [31:0] out_22,
  output [31:0] out_23,
  output [31:0] out_24,
  output [31:0] out_25,
  output [31:0] out_26,
  output [31:0] out_27,
  output [31:0] out_28,
  output [31:0] out_29,
  output [31:0] out_30,
  output [31:0] out_31,
  output [31:0] out_32,
  output [31:0] out_33,
  output [31:0] out_34,
  output [31:0] out_35,
  output [31:0] out_36,
  output [31:0] out_37,
  output [31:0] out_38,
  output [31:0] out_39
);

  wire and_1_out, and_2_out, and_3_out, and_4_out, and_5_out, and_7_out, and_8_out, and_9_out, and_11_out,
       and_12_out, and_13_out, and_14_out, and_15_out, gameprocessor_1_cc, or_1_out, or_2_out, or_3_out,
       s_r_ff_1_q, speedcontroller_1_modclock, ws1, ws2;
  wire [15:0] buffer_1_narrowout, controlled_buffer_1_out, controlled_buffer_3_out, controlled_buffer_5_out,
       Status1_q, Status2_q;
  wire [31:0] wi0, wi1, wi2, wi3, wi4, wi5, wi6, wi7, wi8, wi9, wi10, wi11, wi12, wi13, wi14, wi15, wi16,
       wi17, wi18, wi19, wi20, wi21, wi22, wi23, wi24, wi25, wi26, wi27, wi28, wi29, wi30, wi31;

  and and_1 (and_1_out, I_Osel, I_Oaddr[7]);
  and and_2 (and_2_out, ~in_out_prime, and_1_out);  // AND_Gate
  assign controlled_buffer_1_out = and_2_out ? I_Odat : 16'bz;  // Controlled_Buffer controlled_buffer_1
  or or_1 (or_1_out, reset, and_14_out);
  assign I_Odat_2 = and_3_out ? buffer_1_narrowout : 16'bz;  // Controlled_Buffer controlled_buffer_2
  and and_3 (and_3_out, in_out_prime, and_1_out);
  buffer buffer_1 (
    .sel(and_1_out), .addr(I_Oaddr[6:1]), .narrowin(controlled_buffer_1_out), .rd_wr_prime(in_out_prime),
    .reset(or_1_out), .clock(clock), .in_9(wi0), .in_10(wi1), .in_11(wi2), .in_12(wi3), .in_13(wi4),
    .in_14(wi5), .in_15(wi6), .in_16(wi7), .in_17(wi8), .in_18(wi9), .in_19(wi10), .in_20(wi11),
    .in_21(wi12), .in_22(wi13), .in_23(wi14), .in_24(wi15), .in_25(wi16), .in_26(wi17), .in_27(wi18),
    .in_28(wi19), .in_29(wi20), .in_30(wi21), .in_31(wi22), .in_32(wi23), .in_33(wi24), .in_34(wi25),
    .in_35(wi26), .in_36(wi27), .in_37(wi28), .in_38(wi29), .in_39(wi30), .in_40(wi31),
    .narrowout(buffer_1_narrowout), .out_42(out_8), .out_43(out_9), .out_44(out_10), .out_45(out_11),
    .out_46(out_12), .out_47(out_13), .out_48(out_14), .out_49(out_15), .out_50(out_16), .out_51(out_17),
    .out_52(out_18), .out_53(out_19), .out_54(out_20), .out_55(out_21), .out_56(out_22), .out_57(out_23),
    .out_58(out_24), .out_59(out_25), .out_60(out_26), .out_61(out_27), .out_62(out_28), .out_63(out_29),
    .out_64(out_30), .out_65(out_31), .out_66(out_32), .out_67(out_33), .out_68(out_34), .out_69(out_35),
    .out_70(out_36), .out_71(out_37), .out_72(out_38), .out_73(out_39), .play(or_3_out),
    .cc(gameprocessor_1_cc));
  gameProcessor gameprocessor_1 (
    .cc(gameprocessor_1_cc), .clock(speedcontroller_1_modclock), .play(or_3_out), .surv(Status1_q[8:0]),
    .born(Status2_q[8:0]), .in_7(out_8), .in_8(out_9), .in_9(out_10), .in_10(out_11), .in_11(out_12),
    .in_12(out_13), .in_13(out_14), .in_14(out_15), .in_15(out_16), .in_16(out_17), .in_17(out_18),
    .in_18(out_19), .in_19(out_20), .in_20(out_21), .in_21(out_22), .in_22(out_23), .in_23(out_24),
    .in_24(out_25), .in_25(out_26), .in_26(out_27), .in_27(out_28), .in_28(out_29), .in_29(out_30),
    .in_30(out_31), .in_31(out_32), .in_32(out_33), .in_33(out_34), .in_34(out_35), .in_35(out_36),
    .in_36(out_37), .in_37(out_38), .in_38(out_39), .out_40(wi0), .out_41(wi1), .out_42(wi2), .out_43(wi3),
    .out_44(wi4), .out_45(wi5), .out_46(wi6), .out_47(wi7), .out_48(wi8), .out_49(wi9), .out_50(wi10),
    .out_51(wi11), .out_52(wi12), .out_53(wi13), .out_54(wi14), .out_55(wi15), .out_56(wi16), .out_57(wi17),
    .out_58(wi18), .out_59(wi19), .out_60(wi20), .out_61(wi21), .out_62(wi22), .out_63(wi23), .out_64(wi24),
    .out_65(wi25), .out_66(wi26), .out_67(wi27), .out_68(wi28), .out_69(wi29), .out_70(wi30), .out_71(wi31),
    .reset(or_2_out), .mode(Status1_q[9]));
  speedController speedcontroller_1 (
    .speed(Status2_q[11:10]), .play(or_3_out), .clock(clock), .modClock(speedcontroller_1_modclock));
  or or_2 (or_2_out, reset, ws2, ws1, and_14_out);
  and and_4 (and_4_out, ~I_Oaddr[7], I_Oaddr[6], I_Oaddr[5], I_Oaddr[4], I_Oaddr[3], I_Oaddr[2], I_Oaddr[1], ~I_Oaddr[0]);  // AND_Gate
  and and_5 (and_5_out, I_Osel, and_4_out);
  and and_6 (ws1, ~in_out_prime, and_5_out);  // AND_Gate
  assign controlled_buffer_3_out = ws1 ? I_Odat : 16'bz;  // Controlled_Buffer controlled_buffer_3
  assign I_Odat_2 = and_7_out ? Status1_q : 16'bz;  // Controlled_Buffer controlled_buffer_4
  and and_7 (and_7_out, in_out_prime, and_5_out);
  Register #(.width(16)) Status1 (.D(controlled_buffer_3_out), .en(and_5_out), .Q(Status1_q), .clk(clock), .clr(reset));
  and and_8 (and_8_out, ~I_Oaddr[7], I_Oaddr[6], I_Oaddr[5], I_Oaddr[4], I_Oaddr[3], I_Oaddr[2], ~I_Oaddr[1], ~I_Oaddr[0]);  // AND_Gate
  and and_9 (and_9_out, I_Osel, and_8_out);
  and and_10 (ws2, ~in_out_prime, and_9_out);  // AND_Gate
  assign controlled_buffer_5_out = ws2 ? I_Odat : 16'bz;  // Controlled_Buffer controlled_buffer_5
  assign I_Odat_2 = and_11_out ? Status2_q : 16'bz;  // Controlled_Buffer controlled_buffer_6
  and and_11 (and_11_out, in_out_prime, and_9_out);
  Register #(.width(16)) Status2 (.D(controlled_buffer_5_out), .en(and_9_out), .Q(Status2_q), .clk(clock), .clr(reset));
  or or_3 (or_3_out, Status2_q[9], s_r_ff_1_q);
  and and_12 (and_12_out, ~I_Oaddr[7], I_Oaddr[6], I_Oaddr[5], I_Oaddr[4], ~I_Oaddr[3], I_Oaddr[2], I_Oaddr[1], ~I_Oaddr[0]);  // AND_Gate
  and and_13 (and_13_out, I_Osel, and_12_out);
  and and_14 (and_14_out, I_Osel, and_15_out, clock);
  S_R_Flip_Flop s_r_ff_1 (
    .S(and_13_out), .clk(clock), .R(1'b0), .Q(s_r_ff_1_q), .reset(gameprocessor_1_cc));  // open: Qn, preset, en
  and and_15 (and_15_out, ~I_Oaddr[7], I_Oaddr[6], I_Oaddr[5], I_Oaddr[4], ~I_Oaddr[3], I_Oaddr[2], ~I_Oaddr[1], ~I_Oaddr[0]);  // AND_Gate

  // Other names for the same wires on the sheet: wo0[31:0] = out_8; wo1[31:0] = out_9; wo2[31:0] = out_10;
  //   wo3[31:0] = out_11; wo4[31:0] = out_12; wo5[31:0] = out_13; wo6[31:0] = out_14; wo7[31:0] = out_15;
  //   wo8[31:0] = out_16; wo9[31:0] = out_17; wo10[31:0] = out_18; wo11[31:0] = out_19; wo12[31:0] = out_20;
  //   wo13[31:0] = out_21; wo14[31:0] = out_22; wo15[31:0] = out_23; wo16[31:0] = out_24; wo17[31:0] = out_25;
  //   wo18[31:0] = out_26; wo19[31:0] = out_27; wo20[31:0] = out_28; wo21[31:0] = out_29; wo22[31:0] = out_30;
  //   wo23[31:0] = out_31; wo24[31:0] = out_32; wo25[31:0] = out_33; wo26[31:0] = out_34; wo27[31:0] = out_35;
  //   wo28[31:0] = out_36; wo29[31:0] = out_37; wo30[31:0] = out_38; wo31[31:0] = out_39
endmodule

module buffer (
  input  clock,
  input  sel,
  input  [5:0] addr,
  input  cc,
  input  [15:0] narrowin,
  input  rd_wr_prime,
  input  reset,
  input  play,
  input  [31:0] in_9,
  input  [31:0] in_10,
  input  [31:0] in_11,
  input  [31:0] in_12,
  input  [31:0] in_13,
  input  [31:0] in_14,
  input  [31:0] in_15,
  input  [31:0] in_16,
  input  [31:0] in_17,
  input  [31:0] in_18,
  input  [31:0] in_19,
  input  [31:0] in_20,
  input  [31:0] in_21,
  input  [31:0] in_22,
  input  [31:0] in_23,
  input  [31:0] in_24,
  input  [31:0] in_25,
  input  [31:0] in_26,
  input  [31:0] in_27,
  input  [31:0] in_28,
  input  [31:0] in_29,
  input  [31:0] in_30,
  input  [31:0] in_31,
  input  [31:0] in_32,
  input  [31:0] in_33,
  input  [31:0] in_34,
  input  [31:0] in_35,
  input  [31:0] in_36,
  input  [31:0] in_37,
  input  [31:0] in_38,
  input  [31:0] in_39,
  input  [31:0] in_40,
  output [15:0] narrowout,
  output [31:0] out_42,
  output [31:0] out_43,
  output [31:0] out_44,
  output [31:0] out_45,
  output [31:0] out_46,
  output [31:0] out_47,
  output [31:0] out_48,
  output [31:0] out_49,
  output [31:0] out_50,
  output [31:0] out_51,
  output [31:0] out_52,
  output [31:0] out_53,
  output [31:0] out_54,
  output [31:0] out_55,
  output [31:0] out_56,
  output [31:0] out_57,
  output [31:0] out_58,
  output [31:0] out_59,
  output [31:0] out_60,
  output [31:0] out_61,
  output [31:0] out_62,
  output [31:0] out_63,
  output [31:0] out_64,
  output [31:0] out_65,
  output [31:0] out_66,
  output [31:0] out_67,
  output [31:0] out_68,
  output [31:0] out_69,
  output [31:0] out_70,
  output [31:0] out_71,
  output [31:0] out_72,
  output [31:0] out_73
);

  wire bufferrow_2_block_2, bufferrow_2_countclock_2, bufferrow_2_play_2, bufferrow_2_rd_wr_prime_2,
       bufferrow_2_reset_2, bufferrow_3_block_2, bufferrow_3_countclock_2, bufferrow_3_play_2,
       bufferrow_3_rd_wr_prime_2, bufferrow_3_reset_2, bufferrow_4_block_2, bufferrow_4_countclock_2,
       bufferrow_4_play_2, bufferrow_4_rd_wr_prime_2, bufferrow_4_reset_2, bufferrow_5_block_2,
       bufferrow_5_countclock_2, bufferrow_5_play_2, bufferrow_5_rd_wr_prime_2, bufferrow_5_reset_2,
       bufferrow_6_block_2, bufferrow_6_countclock_2, bufferrow_6_play_2, bufferrow_6_rd_wr_prime_2,
       bufferrow_6_reset_2, bufferrow_7_block_2, bufferrow_7_countclock_2, bufferrow_7_play_2,
       bufferrow_7_rd_wr_prime_2, bufferrow_7_reset_2, bufferrow_8_block_2, bufferrow_8_countclock_2,
       bufferrow_8_play_2, bufferrow_8_rd_wr_prime_2, bufferrow_8_reset_2, bufferrow_9_block_2,
       bufferrow_9_countclock_2, bufferrow_9_play_2, bufferrow_9_rd_wr_prime_2, bufferrow_9_reset_2,
       bufferrow_10_block_2, bufferrow_10_countclock_2, bufferrow_10_play_2, bufferrow_10_rd_wr_prime_2,
       bufferrow_10_reset_2, bufferrow_11_block_2, bufferrow_11_countclock_2, bufferrow_11_play_2,
       bufferrow_11_rd_wr_prime_2, bufferrow_11_reset_2, bufferrow_12_block_2, bufferrow_12_countclock_2,
       bufferrow_12_play_2, bufferrow_12_rd_wr_prime_2, bufferrow_12_reset_2, bufferrow_13_block_2,
       bufferrow_13_countclock_2, bufferrow_13_play_2, bufferrow_13_rd_wr_prime_2, bufferrow_13_reset_2,
       bufferrow_14_block_2, bufferrow_14_countclock_2, bufferrow_14_play_2, bufferrow_14_rd_wr_prime_2,
       bufferrow_14_reset_2, bufferrow_15_block_2, bufferrow_15_countclock_2, bufferrow_15_play_2,
       bufferrow_15_rd_wr_prime_2, bufferrow_15_reset_2, bufferrow_16_block_2, bufferrow_16_countclock_2,
       bufferrow_16_play_2, bufferrow_16_rd_wr_prime_2, bufferrow_16_reset_2, bufferrow_17_block_2,
       bufferrow_17_countclock_2, bufferrow_17_play_2, bufferrow_17_rd_wr_prime_2, bufferrow_17_reset_2,
       bufferrow_18_block_2, bufferrow_18_countclock_2, bufferrow_18_play_2, bufferrow_18_rd_wr_prime_2,
       bufferrow_18_reset_2, bufferrow_19_block_2, bufferrow_19_countclock_2, bufferrow_19_play_2,
       bufferrow_19_rd_wr_prime_2, bufferrow_19_reset_2, bufferrow_20_block_2, bufferrow_20_countclock_2,
       bufferrow_20_play_2, bufferrow_20_rd_wr_prime_2, bufferrow_20_reset_2, bufferrow_21_block_2,
       bufferrow_21_countclock_2, bufferrow_21_play_2, bufferrow_21_rd_wr_prime_2, bufferrow_21_reset_2,
       bufferrow_22_block_2, bufferrow_22_countclock_2, bufferrow_22_play_2, bufferrow_22_rd_wr_prime_2,
       bufferrow_22_reset_2, bufferrow_23_block_2, bufferrow_23_countclock_2, bufferrow_23_play_2,
       bufferrow_23_rd_wr_prime_2, bufferrow_23_reset_2, bufferrow_24_block_2, bufferrow_24_countclock_2,
       bufferrow_24_play_2, bufferrow_24_rd_wr_prime_2, bufferrow_24_reset_2, bufferrow_25_block_2,
       bufferrow_25_countclock_2, bufferrow_25_play_2, bufferrow_25_rd_wr_prime_2, bufferrow_25_reset_2,
       bufferrow_26_block_2, bufferrow_26_countclock_2, bufferrow_26_play_2, bufferrow_26_rd_wr_prime_2,
       bufferrow_26_reset_2, bufferrow_27_block_2, bufferrow_27_countclock_2, bufferrow_27_play_2,
       bufferrow_27_rd_wr_prime_2, bufferrow_27_reset_2, bufferrow_28_block_2, bufferrow_28_countclock_2,
       bufferrow_28_play_2, bufferrow_28_rd_wr_prime_2, bufferrow_28_reset_2, bufferrow_29_block_2,
       bufferrow_29_countclock_2, bufferrow_29_play_2, bufferrow_29_rd_wr_prime_2, bufferrow_29_reset_2,
       bufferrow_30_block_2, bufferrow_30_countclock_2, bufferrow_30_play_2, bufferrow_30_rd_wr_prime_2,
       bufferrow_30_reset_2, bufferrow_31_block_2, bufferrow_31_countclock_2, bufferrow_31_play_2,
       bufferrow_31_rd_wr_prime_2, bufferrow_31_reset_2, bufferrow_32_block_2, bufferrow_32_countclock_2,
       bufferrow_32_play_2, bufferrow_32_rd_wr_prime_2, bufferrow_32_reset_2;
  wire [31:0] decoder_1_out0, demultiplexer_1_out0;

  Decoder #(.select(5), .disabled(0)) decoder_1 (
    .out0(decoder_1_out0[0]), .out1(decoder_1_out0[1]), .out2(decoder_1_out0[2]), .out3(decoder_1_out0[3]),
    .out4(decoder_1_out0[4]), .out5(decoder_1_out0[5]), .out6(decoder_1_out0[6]), .out7(decoder_1_out0[7]),
    .out8(decoder_1_out0[8]), .out9(decoder_1_out0[9]), .out10(decoder_1_out0[10]),
    .out11(decoder_1_out0[11]), .out12(decoder_1_out0[12]), .out13(decoder_1_out0[13]),
    .out14(decoder_1_out0[14]), .out15(decoder_1_out0[15]), .out16(decoder_1_out0[16]),
    .out17(decoder_1_out0[17]), .out18(decoder_1_out0[18]), .out19(decoder_1_out0[19]),
    .out20(decoder_1_out0[20]), .out21(decoder_1_out0[21]), .out22(decoder_1_out0[22]),
    .out23(decoder_1_out0[23]), .out24(decoder_1_out0[24]), .out25(decoder_1_out0[25]),
    .out26(decoder_1_out0[26]), .out27(decoder_1_out0[27]), .out28(decoder_1_out0[28]),
    .out29(decoder_1_out0[29]), .out30(decoder_1_out0[30]), .out31(decoder_1_out0[31]), .sel(addr[5:1]),
    .en(sel));
  bufferrow bufferrow_1 (
    .widein(in_9), .narrowin(narrowin), .rd_wr_prime(bufferrow_2_rd_wr_prime_2), .sel(decoder_1_out0[0]),
    .block(bufferrow_2_block_2), .reset(bufferrow_2_reset_2), .clock(demultiplexer_1_out0[0]),
    .narrowout(narrowout), .wideout(out_42), .countclock(bufferrow_2_countclock_2), .play(bufferrow_2_play_2));  // open: block_2, rd_wr_prime_2, reset_2, countclock_2, play_2
  bufferrow bufferrow_2 (
    .widein(in_10), .narrowin(narrowin), .rd_wr_prime(bufferrow_3_rd_wr_prime_2), .sel(decoder_1_out0[1]),
    .block(bufferrow_3_block_2), .reset(bufferrow_3_reset_2), .clock(demultiplexer_1_out0[1]),
    .narrowout(narrowout), .wideout(out_43), .block_2(bufferrow_2_block_2),
    .rd_wr_prime_2(bufferrow_2_rd_wr_prime_2), .reset_2(bufferrow_2_reset_2),
    .countclock(bufferrow_3_countclock_2), .countclock_2(bufferrow_2_countclock_2),
    .play(bufferrow_3_play_2), .play_2(bufferrow_2_play_2));
  bufferrow bufferrow_3 (
    .widein(in_11), .narrowin(narrowin), .rd_wr_prime(bufferrow_4_rd_wr_prime_2), .sel(decoder_1_out0[2]),
    .block(bufferrow_4_block_2), .reset(bufferrow_4_reset_2), .clock(demultiplexer_1_out0[2]),
    .narrowout(narrowout), .wideout(out_44), .block_2(bufferrow_3_block_2),
    .rd_wr_prime_2(bufferrow_3_rd_wr_prime_2), .reset_2(bufferrow_3_reset_2),
    .countclock(bufferrow_4_countclock_2), .countclock_2(bufferrow_3_countclock_2),
    .play(bufferrow_4_play_2), .play_2(bufferrow_3_play_2));
  bufferrow bufferrow_4 (
    .widein(in_12), .narrowin(narrowin), .rd_wr_prime(bufferrow_5_rd_wr_prime_2), .sel(decoder_1_out0[3]),
    .block(bufferrow_5_block_2), .reset(bufferrow_5_reset_2), .clock(demultiplexer_1_out0[3]),
    .narrowout(narrowout), .wideout(out_45), .block_2(bufferrow_4_block_2),
    .rd_wr_prime_2(bufferrow_4_rd_wr_prime_2), .reset_2(bufferrow_4_reset_2),
    .countclock(bufferrow_5_countclock_2), .countclock_2(bufferrow_4_countclock_2),
    .play(bufferrow_5_play_2), .play_2(bufferrow_4_play_2));
  bufferrow bufferrow_5 (
    .widein(in_13), .narrowin(narrowin), .rd_wr_prime(bufferrow_6_rd_wr_prime_2), .sel(decoder_1_out0[4]),
    .block(bufferrow_6_block_2), .reset(bufferrow_6_reset_2), .clock(demultiplexer_1_out0[4]),
    .narrowout(narrowout), .wideout(out_46), .block_2(bufferrow_5_block_2),
    .rd_wr_prime_2(bufferrow_5_rd_wr_prime_2), .reset_2(bufferrow_5_reset_2),
    .countclock(bufferrow_6_countclock_2), .countclock_2(bufferrow_5_countclock_2),
    .play(bufferrow_6_play_2), .play_2(bufferrow_5_play_2));
  bufferrow bufferrow_6 (
    .widein(in_14), .narrowin(narrowin), .rd_wr_prime(bufferrow_7_rd_wr_prime_2), .sel(decoder_1_out0[5]),
    .block(bufferrow_7_block_2), .reset(bufferrow_7_reset_2), .clock(demultiplexer_1_out0[5]),
    .narrowout(narrowout), .wideout(out_47), .block_2(bufferrow_6_block_2),
    .rd_wr_prime_2(bufferrow_6_rd_wr_prime_2), .reset_2(bufferrow_6_reset_2),
    .countclock(bufferrow_7_countclock_2), .countclock_2(bufferrow_6_countclock_2),
    .play(bufferrow_7_play_2), .play_2(bufferrow_6_play_2));
  bufferrow bufferrow_7 (
    .widein(in_15), .narrowin(narrowin), .rd_wr_prime(bufferrow_8_rd_wr_prime_2), .sel(decoder_1_out0[6]),
    .block(bufferrow_8_block_2), .reset(bufferrow_8_reset_2), .clock(demultiplexer_1_out0[6]),
    .narrowout(narrowout), .wideout(out_48), .block_2(bufferrow_7_block_2),
    .rd_wr_prime_2(bufferrow_7_rd_wr_prime_2), .reset_2(bufferrow_7_reset_2),
    .countclock(bufferrow_8_countclock_2), .countclock_2(bufferrow_7_countclock_2),
    .play(bufferrow_8_play_2), .play_2(bufferrow_7_play_2));
  bufferrow bufferrow_8 (
    .widein(in_16), .narrowin(narrowin), .rd_wr_prime(bufferrow_9_rd_wr_prime_2), .sel(decoder_1_out0[7]),
    .block(bufferrow_9_block_2), .reset(bufferrow_9_reset_2), .clock(demultiplexer_1_out0[7]),
    .narrowout(narrowout), .wideout(out_49), .block_2(bufferrow_8_block_2),
    .rd_wr_prime_2(bufferrow_8_rd_wr_prime_2), .reset_2(bufferrow_8_reset_2),
    .countclock(bufferrow_9_countclock_2), .countclock_2(bufferrow_8_countclock_2),
    .play(bufferrow_9_play_2), .play_2(bufferrow_8_play_2));
  bufferrow bufferrow_9 (
    .widein(in_17), .narrowin(narrowin), .rd_wr_prime(bufferrow_10_rd_wr_prime_2), .sel(decoder_1_out0[8]),
    .block(bufferrow_10_block_2), .reset(bufferrow_10_reset_2), .clock(demultiplexer_1_out0[8]),
    .narrowout(narrowout), .wideout(out_50), .block_2(bufferrow_9_block_2),
    .rd_wr_prime_2(bufferrow_9_rd_wr_prime_2), .reset_2(bufferrow_9_reset_2),
    .countclock(bufferrow_10_countclock_2), .countclock_2(bufferrow_9_countclock_2),
    .play(bufferrow_10_play_2), .play_2(bufferrow_9_play_2));
  bufferrow bufferrow_10 (
    .widein(in_18), .narrowin(narrowin), .rd_wr_prime(bufferrow_11_rd_wr_prime_2), .sel(decoder_1_out0[9]),
    .block(bufferrow_11_block_2), .reset(bufferrow_11_reset_2), .clock(demultiplexer_1_out0[9]),
    .narrowout(narrowout), .wideout(out_51), .block_2(bufferrow_10_block_2),
    .rd_wr_prime_2(bufferrow_10_rd_wr_prime_2), .reset_2(bufferrow_10_reset_2),
    .countclock(bufferrow_11_countclock_2), .countclock_2(bufferrow_10_countclock_2),
    .play(bufferrow_11_play_2), .play_2(bufferrow_10_play_2));
  bufferrow bufferrow_11 (
    .widein(in_19), .narrowin(narrowin), .rd_wr_prime(bufferrow_12_rd_wr_prime_2), .sel(decoder_1_out0[10]),
    .block(bufferrow_12_block_2), .reset(bufferrow_12_reset_2), .clock(demultiplexer_1_out0[10]),
    .narrowout(narrowout), .wideout(out_52), .block_2(bufferrow_11_block_2),
    .rd_wr_prime_2(bufferrow_11_rd_wr_prime_2), .reset_2(bufferrow_11_reset_2),
    .countclock(bufferrow_12_countclock_2), .countclock_2(bufferrow_11_countclock_2),
    .play(bufferrow_12_play_2), .play_2(bufferrow_11_play_2));
  bufferrow bufferrow_12 (
    .widein(in_20), .narrowin(narrowin), .rd_wr_prime(bufferrow_13_rd_wr_prime_2), .sel(decoder_1_out0[11]),
    .block(bufferrow_13_block_2), .reset(bufferrow_13_reset_2), .clock(demultiplexer_1_out0[11]),
    .narrowout(narrowout), .wideout(out_53), .block_2(bufferrow_12_block_2),
    .rd_wr_prime_2(bufferrow_12_rd_wr_prime_2), .reset_2(bufferrow_12_reset_2),
    .countclock(bufferrow_13_countclock_2), .countclock_2(bufferrow_12_countclock_2),
    .play(bufferrow_13_play_2), .play_2(bufferrow_12_play_2));
  bufferrow bufferrow_13 (
    .widein(in_21), .narrowin(narrowin), .rd_wr_prime(bufferrow_14_rd_wr_prime_2), .sel(decoder_1_out0[12]),
    .block(bufferrow_14_block_2), .reset(bufferrow_14_reset_2), .clock(demultiplexer_1_out0[12]),
    .narrowout(narrowout), .wideout(out_54), .block_2(bufferrow_13_block_2),
    .rd_wr_prime_2(bufferrow_13_rd_wr_prime_2), .reset_2(bufferrow_13_reset_2),
    .countclock(bufferrow_14_countclock_2), .countclock_2(bufferrow_13_countclock_2),
    .play(bufferrow_14_play_2), .play_2(bufferrow_13_play_2));
  bufferrow bufferrow_14 (
    .widein(in_22), .narrowin(narrowin), .rd_wr_prime(bufferrow_15_rd_wr_prime_2), .sel(decoder_1_out0[13]),
    .block(bufferrow_15_block_2), .reset(bufferrow_15_reset_2), .clock(demultiplexer_1_out0[13]),
    .narrowout(narrowout), .wideout(out_55), .block_2(bufferrow_14_block_2),
    .rd_wr_prime_2(bufferrow_14_rd_wr_prime_2), .reset_2(bufferrow_14_reset_2),
    .countclock(bufferrow_15_countclock_2), .countclock_2(bufferrow_14_countclock_2),
    .play(bufferrow_15_play_2), .play_2(bufferrow_14_play_2));
  bufferrow bufferrow_15 (
    .widein(in_23), .narrowin(narrowin), .rd_wr_prime(bufferrow_16_rd_wr_prime_2), .sel(decoder_1_out0[14]),
    .block(bufferrow_16_block_2), .reset(bufferrow_16_reset_2), .clock(demultiplexer_1_out0[14]),
    .narrowout(narrowout), .wideout(out_56), .block_2(bufferrow_15_block_2),
    .rd_wr_prime_2(bufferrow_15_rd_wr_prime_2), .reset_2(bufferrow_15_reset_2),
    .countclock(bufferrow_16_countclock_2), .countclock_2(bufferrow_15_countclock_2),
    .play(bufferrow_16_play_2), .play_2(bufferrow_15_play_2));
  bufferrow bufferrow_16 (
    .widein(in_24), .narrowin(narrowin), .rd_wr_prime(bufferrow_17_rd_wr_prime_2), .sel(decoder_1_out0[15]),
    .block(bufferrow_17_block_2), .reset(bufferrow_17_reset_2), .clock(demultiplexer_1_out0[15]),
    .narrowout(narrowout), .wideout(out_57), .block_2(bufferrow_16_block_2),
    .rd_wr_prime_2(bufferrow_16_rd_wr_prime_2), .reset_2(bufferrow_16_reset_2),
    .countclock(bufferrow_17_countclock_2), .countclock_2(bufferrow_16_countclock_2),
    .play(bufferrow_17_play_2), .play_2(bufferrow_16_play_2));
  bufferrow bufferrow_17 (
    .widein(in_25), .narrowin(narrowin), .rd_wr_prime(bufferrow_18_rd_wr_prime_2), .sel(decoder_1_out0[16]),
    .block(bufferrow_18_block_2), .reset(bufferrow_18_reset_2), .clock(demultiplexer_1_out0[16]),
    .narrowout(narrowout), .wideout(out_58), .block_2(bufferrow_17_block_2),
    .rd_wr_prime_2(bufferrow_17_rd_wr_prime_2), .reset_2(bufferrow_17_reset_2),
    .countclock(bufferrow_18_countclock_2), .countclock_2(bufferrow_17_countclock_2),
    .play(bufferrow_18_play_2), .play_2(bufferrow_17_play_2));
  bufferrow bufferrow_18 (
    .widein(in_26), .narrowin(narrowin), .rd_wr_prime(bufferrow_19_rd_wr_prime_2), .sel(decoder_1_out0[17]),
    .block(bufferrow_19_block_2), .reset(bufferrow_19_reset_2), .clock(demultiplexer_1_out0[17]),
    .narrowout(narrowout), .wideout(out_59), .block_2(bufferrow_18_block_2),
    .rd_wr_prime_2(bufferrow_18_rd_wr_prime_2), .reset_2(bufferrow_18_reset_2),
    .countclock(bufferrow_19_countclock_2), .countclock_2(bufferrow_18_countclock_2),
    .play(bufferrow_19_play_2), .play_2(bufferrow_18_play_2));
  bufferrow bufferrow_19 (
    .widein(in_27), .narrowin(narrowin), .rd_wr_prime(bufferrow_20_rd_wr_prime_2), .sel(decoder_1_out0[18]),
    .block(bufferrow_20_block_2), .reset(bufferrow_20_reset_2), .clock(demultiplexer_1_out0[18]),
    .narrowout(narrowout), .wideout(out_60), .block_2(bufferrow_19_block_2),
    .rd_wr_prime_2(bufferrow_19_rd_wr_prime_2), .reset_2(bufferrow_19_reset_2),
    .countclock(bufferrow_20_countclock_2), .countclock_2(bufferrow_19_countclock_2),
    .play(bufferrow_20_play_2), .play_2(bufferrow_19_play_2));
  bufferrow bufferrow_20 (
    .widein(in_28), .narrowin(narrowin), .rd_wr_prime(bufferrow_21_rd_wr_prime_2), .sel(decoder_1_out0[19]),
    .block(bufferrow_21_block_2), .reset(bufferrow_21_reset_2), .clock(demultiplexer_1_out0[19]),
    .narrowout(narrowout), .wideout(out_61), .block_2(bufferrow_20_block_2),
    .rd_wr_prime_2(bufferrow_20_rd_wr_prime_2), .reset_2(bufferrow_20_reset_2),
    .countclock(bufferrow_21_countclock_2), .countclock_2(bufferrow_20_countclock_2),
    .play(bufferrow_21_play_2), .play_2(bufferrow_20_play_2));
  bufferrow bufferrow_21 (
    .widein(in_29), .narrowin(narrowin), .rd_wr_prime(bufferrow_22_rd_wr_prime_2), .sel(decoder_1_out0[20]),
    .block(bufferrow_22_block_2), .reset(bufferrow_22_reset_2), .clock(demultiplexer_1_out0[20]),
    .narrowout(narrowout), .wideout(out_62), .block_2(bufferrow_21_block_2),
    .rd_wr_prime_2(bufferrow_21_rd_wr_prime_2), .reset_2(bufferrow_21_reset_2),
    .countclock(bufferrow_22_countclock_2), .countclock_2(bufferrow_21_countclock_2),
    .play(bufferrow_22_play_2), .play_2(bufferrow_21_play_2));
  bufferrow bufferrow_22 (
    .widein(in_30), .narrowin(narrowin), .rd_wr_prime(bufferrow_23_rd_wr_prime_2), .sel(decoder_1_out0[21]),
    .block(bufferrow_23_block_2), .reset(bufferrow_23_reset_2), .clock(demultiplexer_1_out0[21]),
    .narrowout(narrowout), .wideout(out_63), .block_2(bufferrow_22_block_2),
    .rd_wr_prime_2(bufferrow_22_rd_wr_prime_2), .reset_2(bufferrow_22_reset_2),
    .countclock(bufferrow_23_countclock_2), .countclock_2(bufferrow_22_countclock_2),
    .play(bufferrow_23_play_2), .play_2(bufferrow_22_play_2));
  bufferrow bufferrow_23 (
    .widein(in_31), .narrowin(narrowin), .rd_wr_prime(bufferrow_24_rd_wr_prime_2), .sel(decoder_1_out0[22]),
    .block(bufferrow_24_block_2), .reset(bufferrow_24_reset_2), .clock(demultiplexer_1_out0[22]),
    .narrowout(narrowout), .wideout(out_64), .block_2(bufferrow_23_block_2),
    .rd_wr_prime_2(bufferrow_23_rd_wr_prime_2), .reset_2(bufferrow_23_reset_2),
    .countclock(bufferrow_24_countclock_2), .countclock_2(bufferrow_23_countclock_2),
    .play(bufferrow_24_play_2), .play_2(bufferrow_23_play_2));
  bufferrow bufferrow_24 (
    .widein(in_32), .narrowin(narrowin), .rd_wr_prime(bufferrow_25_rd_wr_prime_2), .sel(decoder_1_out0[23]),
    .block(bufferrow_25_block_2), .reset(bufferrow_25_reset_2), .clock(demultiplexer_1_out0[23]),
    .narrowout(narrowout), .wideout(out_65), .block_2(bufferrow_24_block_2),
    .rd_wr_prime_2(bufferrow_24_rd_wr_prime_2), .reset_2(bufferrow_24_reset_2),
    .countclock(bufferrow_25_countclock_2), .countclock_2(bufferrow_24_countclock_2),
    .play(bufferrow_25_play_2), .play_2(bufferrow_24_play_2));
  bufferrow bufferrow_25 (
    .widein(in_33), .narrowin(narrowin), .rd_wr_prime(bufferrow_26_rd_wr_prime_2), .sel(decoder_1_out0[24]),
    .block(bufferrow_26_block_2), .reset(bufferrow_26_reset_2), .clock(demultiplexer_1_out0[24]),
    .narrowout(narrowout), .wideout(out_66), .block_2(bufferrow_25_block_2),
    .rd_wr_prime_2(bufferrow_25_rd_wr_prime_2), .reset_2(bufferrow_25_reset_2),
    .countclock(bufferrow_26_countclock_2), .countclock_2(bufferrow_25_countclock_2),
    .play(bufferrow_26_play_2), .play_2(bufferrow_25_play_2));
  bufferrow bufferrow_26 (
    .widein(in_34), .narrowin(narrowin), .rd_wr_prime(bufferrow_27_rd_wr_prime_2), .sel(decoder_1_out0[25]),
    .block(bufferrow_27_block_2), .reset(bufferrow_27_reset_2), .clock(demultiplexer_1_out0[25]),
    .narrowout(narrowout), .wideout(out_67), .block_2(bufferrow_26_block_2),
    .rd_wr_prime_2(bufferrow_26_rd_wr_prime_2), .reset_2(bufferrow_26_reset_2),
    .countclock(bufferrow_27_countclock_2), .countclock_2(bufferrow_26_countclock_2),
    .play(bufferrow_27_play_2), .play_2(bufferrow_26_play_2));
  bufferrow bufferrow_27 (
    .widein(in_35), .narrowin(narrowin), .rd_wr_prime(bufferrow_28_rd_wr_prime_2), .sel(decoder_1_out0[26]),
    .block(bufferrow_28_block_2), .reset(bufferrow_28_reset_2), .clock(demultiplexer_1_out0[26]),
    .narrowout(narrowout), .wideout(out_68), .block_2(bufferrow_27_block_2),
    .rd_wr_prime_2(bufferrow_27_rd_wr_prime_2), .reset_2(bufferrow_27_reset_2),
    .countclock(bufferrow_28_countclock_2), .countclock_2(bufferrow_27_countclock_2),
    .play(bufferrow_28_play_2), .play_2(bufferrow_27_play_2));
  bufferrow bufferrow_28 (
    .widein(in_36), .narrowin(narrowin), .rd_wr_prime(bufferrow_29_rd_wr_prime_2), .sel(decoder_1_out0[27]),
    .block(bufferrow_29_block_2), .reset(bufferrow_29_reset_2), .clock(demultiplexer_1_out0[27]),
    .narrowout(narrowout), .wideout(out_69), .block_2(bufferrow_28_block_2),
    .rd_wr_prime_2(bufferrow_28_rd_wr_prime_2), .reset_2(bufferrow_28_reset_2),
    .countclock(bufferrow_29_countclock_2), .countclock_2(bufferrow_28_countclock_2),
    .play(bufferrow_29_play_2), .play_2(bufferrow_28_play_2));
  bufferrow bufferrow_29 (
    .widein(in_37), .narrowin(narrowin), .rd_wr_prime(bufferrow_30_rd_wr_prime_2), .sel(decoder_1_out0[28]),
    .block(bufferrow_30_block_2), .reset(bufferrow_30_reset_2), .clock(demultiplexer_1_out0[28]),
    .narrowout(narrowout), .wideout(out_70), .block_2(bufferrow_29_block_2),
    .rd_wr_prime_2(bufferrow_29_rd_wr_prime_2), .reset_2(bufferrow_29_reset_2),
    .countclock(bufferrow_30_countclock_2), .countclock_2(bufferrow_29_countclock_2),
    .play(bufferrow_30_play_2), .play_2(bufferrow_29_play_2));
  bufferrow bufferrow_30 (
    .widein(in_38), .narrowin(narrowin), .rd_wr_prime(bufferrow_31_rd_wr_prime_2), .sel(decoder_1_out0[29]),
    .block(bufferrow_31_block_2), .reset(bufferrow_31_reset_2), .clock(demultiplexer_1_out0[29]),
    .narrowout(narrowout), .wideout(out_71), .block_2(bufferrow_30_block_2),
    .rd_wr_prime_2(bufferrow_30_rd_wr_prime_2), .reset_2(bufferrow_30_reset_2),
    .countclock(bufferrow_31_countclock_2), .countclock_2(bufferrow_30_countclock_2),
    .play(bufferrow_31_play_2), .play_2(bufferrow_30_play_2));
  bufferrow bufferrow_31 (
    .widein(in_39), .narrowin(narrowin), .rd_wr_prime(bufferrow_32_rd_wr_prime_2), .sel(decoder_1_out0[30]),
    .block(bufferrow_32_block_2), .reset(bufferrow_32_reset_2), .clock(demultiplexer_1_out0[30]),
    .narrowout(narrowout), .wideout(out_72), .block_2(bufferrow_31_block_2),
    .rd_wr_prime_2(bufferrow_31_rd_wr_prime_2), .reset_2(bufferrow_31_reset_2),
    .countclock(bufferrow_32_countclock_2), .countclock_2(bufferrow_31_countclock_2),
    .play(bufferrow_32_play_2), .play_2(bufferrow_31_play_2));
  bufferrow bufferrow_32 (
    .widein(in_40), .narrowin(narrowin), .rd_wr_prime(rd_wr_prime), .sel(decoder_1_out0[31]),
    .block(addr[0]), .reset(reset), .clock(demultiplexer_1_out0[31]), .narrowout(narrowout),
    .wideout(out_73), .block_2(bufferrow_32_block_2), .rd_wr_prime_2(bufferrow_32_rd_wr_prime_2),
    .reset_2(bufferrow_32_reset_2), .countclock(cc), .countclock_2(bufferrow_32_countclock_2), .play(play),
    .play_2(bufferrow_32_play_2));
  Demultiplexer #(.select(5), .disabled(0)) demultiplexer_1 (
    .out0(demultiplexer_1_out0[0]), .out1(demultiplexer_1_out0[1]), .out2(demultiplexer_1_out0[2]),
    .out3(demultiplexer_1_out0[3]), .out4(demultiplexer_1_out0[4]), .out5(demultiplexer_1_out0[5]),
    .out6(demultiplexer_1_out0[6]), .out7(demultiplexer_1_out0[7]), .out8(demultiplexer_1_out0[8]),
    .out9(demultiplexer_1_out0[9]), .out10(demultiplexer_1_out0[10]), .out11(demultiplexer_1_out0[11]),
    .out12(demultiplexer_1_out0[12]), .out13(demultiplexer_1_out0[13]), .out14(demultiplexer_1_out0[14]),
    .out15(demultiplexer_1_out0[15]), .out16(demultiplexer_1_out0[16]), .out17(demultiplexer_1_out0[17]),
    .out18(demultiplexer_1_out0[18]), .out19(demultiplexer_1_out0[19]), .out20(demultiplexer_1_out0[20]),
    .out21(demultiplexer_1_out0[21]), .out22(demultiplexer_1_out0[22]), .out23(demultiplexer_1_out0[23]),
    .out24(demultiplexer_1_out0[24]), .out25(demultiplexer_1_out0[25]), .out26(demultiplexer_1_out0[26]),
    .out27(demultiplexer_1_out0[27]), .out28(demultiplexer_1_out0[28]), .out29(demultiplexer_1_out0[29]),
    .out30(demultiplexer_1_out0[30]), .out31(demultiplexer_1_out0[31]), .in(clock), .sel(addr[5:1]), .en(sel));

  // Other names for the same wires on the sheet: addr_t[4:0] = addr[5:1]; wi0[31:0] = in_9; wi1[31:0] = in_10;
  //   wi2[31:0] = in_11; wi3[31:0] = in_12; wi4[31:0] = in_13; wi5[31:0] = in_14; wi6[31:0] = in_15;
  //   wi7[31:0] = in_16; wi8[31:0] = in_17; wi9[31:0] = in_18; wi10[31:0] = in_19; wi11[31:0] = in_20;
  //   wi12[31:0] = in_21; wi13[31:0] = in_22; wi14[31:0] = in_23; wi15[31:0] = in_24; wi16[31:0] = in_25;
  //   wi17[31:0] = in_26; wi18[31:0] = in_27; wi19[31:0] = in_28; wi20[31:0] = in_29; wi21[31:0] = in_30;
  //   wi22[31:0] = in_31; wi23[31:0] = in_32; wi24[31:0] = in_33; wi25[31:0] = in_34; wi26[31:0] = in_35;
  //   wi27[31:0] = in_36; wi28[31:0] = in_37; wi29[31:0] = in_38; wi30[31:0] = in_39; wi31[31:0] = in_40;
  //   wo0[31:0] = out_42; wo1[31:0] = out_43; wo2[31:0] = out_44; wo3[31:0] = out_45; wo4[31:0] = out_46;
  //   wo5[31:0] = out_47; wo6[31:0] = out_48; wo7[31:0] = out_49; wo8[31:0] = out_50; wo9[31:0] = out_51;
  //   wo10[31:0] = out_52; wo11[31:0] = out_53; wo12[31:0] = out_54; wo13[31:0] = out_55; wo14[31:0] = out_56;
  //   wo15[31:0] = out_57; wo16[31:0] = out_58; wo17[31:0] = out_59; wo18[31:0] = out_60; wo19[31:0] = out_61;
  //   wo20[31:0] = out_62; wo21[31:0] = out_63; wo22[31:0] = out_64; wo23[31:0] = out_65; wo24[31:0] = out_66;
  //   wo25[31:0] = out_67; wo26[31:0] = out_68; wo27[31:0] = out_69; wo28[31:0] = out_70; wo29[31:0] = out_71;
  //   wo30[31:0] = out_72; wo31[31:0] = out_73
endmodule

module bufferrow (
  input  clock,
  input  [31:0] widein,
  input  sel,
  input  rd_wr_prime,
  input  reset,
  input  block,
  input  countclock,
  input  play,
  input  [15:0] narrowin,
  output [31:0] wideout,
  output reset_2,
  output rd_wr_prime_2,
  output block_2,
  output countclock_2,
  output play_2,
  output [15:0] narrowout
);

  wire and_1_out, and_2_out, and_3_out, and_4_out, not_1_out, not_2_out, or_1_out, or_2_out;
  wire [15:0] controlled_buffer_1_out, controlled_buffer_2_out, controlled_buffer_4_out,
       controlled_buffer_6_out, controlled_buffer_6_out_2;
  wire [31:0] multiplexer_1_out;

  assign controlled_buffer_1_out = and_1_out ? narrowin : 16'bz;  // Controlled_Buffer controlled_buffer_1
  and and_1 (and_1_out, sel, ~rd_wr_prime);  // AND_Gate
  assign controlled_buffer_2_out = not_1_out ? controlled_buffer_1_out : 16'bz;  // Controlled_Buffer controlled_buffer_2
  assign controlled_buffer_2_out = block ? controlled_buffer_6_out_2 : 16'bz;  // Controlled_Buffer controlled_buffer_3
  or or_1 (or_1_out, countclock, clock);
  not not_1 (not_1_out, block);
  and and_2 (and_2_out, ~rd_wr_prime, sel);  // AND_Gate
  or or_2 (or_2_out, and_2_out, play);
  Multiplexer #(.width(32)) multiplexer_1 (
    .in0(widein), .in1({controlled_buffer_2_out, controlled_buffer_4_out}), .out(multiplexer_1_out),
    .sel(sel), .en(or_2_out));
  assign controlled_buffer_4_out = block ? controlled_buffer_1_out : 16'bz;  // Controlled_Buffer controlled_buffer_4
  assign controlled_buffer_4_out = not_2_out ? controlled_buffer_6_out : 16'bz;  // Controlled_Buffer controlled_buffer_5
  not not_2 (not_2_out, block);
  Register #(.width(32)) register_1 (.D(multiplexer_1_out), .en(or_2_out), .Q(wideout), .clk(or_1_out), .clr(reset));
  assign {controlled_buffer_6_out_2, controlled_buffer_6_out} = and_3_out ? wideout : 32'bz;  // Controlled_Buffer controlled_buffer_6
  and and_3 (and_3_out, sel, ~rd_wr_prime);  // AND_Gate
  and and_4 (and_4_out, rd_wr_prime, sel);
  Multiplexer #(.width(16)) multiplexer_2 (
    .in0(wideout[31:16]), .in1(wideout[15:0]), .out(narrowout), .sel(block), .en(and_4_out));

  assign block_2 = block;
  assign countclock_2 = countclock;
  assign play_2 = play;
  assign rd_wr_prime_2 = rd_wr_prime;
  assign reset_2 = reset;

  // Other names for the same wires on the sheet: self[31:0] = wideout; cc = countclock
endmodule

module gameProcessorrow (
  input  [31:0] above,
  input  [8:0] surv,
  input  [8:0] born,
  input  mode,
  input  [31:0] \this ,
  input  [31:0] below,
  output [31:0] out_7
);

  wire and_1_out, and_2_out, and_3_out, and_4_out, and_5_out, and_6_out, cell_1_curr_2, cell_2_curr,
       cell_2_curr_2, cell_3_curr, cell_3_curr_2, cell_4_curr, cell_4_curr_2, cell_5_curr, cell_5_curr_2,
       cell_6_curr, cell_6_curr_2, cell_7_curr, cell_7_curr_2, cell_8_curr, cell_8_curr_2, cell_9_curr,
       cell_9_curr_2, cell_10_curr, cell_10_curr_2, cell_11_curr, cell_11_curr_2, cell_12_curr,
       cell_12_curr_2, cell_13_curr, cell_13_curr_2, cell_14_curr, cell_14_curr_2, cell_15_curr,
       cell_15_curr_2, cell_16_curr, cell_16_curr_2, cell_17_curr, cell_17_curr_2, cell_18_curr,
       cell_18_curr_2, cell_19_curr, cell_19_curr_2, cell_20_curr, cell_20_curr_2, cell_21_curr,
       cell_21_curr_2, cell_22_curr, cell_22_curr_2, cell_23_curr, cell_23_curr_2, cell_24_curr,
       cell_24_curr_2, cell_25_curr, cell_25_curr_2, cell_26_curr, cell_26_curr_2, cell_27_curr,
       cell_27_curr_2, cell_28_curr, cell_28_curr_2, cell_29_curr, cell_29_curr_2, cell_30_curr,
       cell_30_curr_2, cell_31_curr, cell_31_curr_2, cell_32_curr;
  wire [8:0] cell_1_born_2, cell_1_surv_2, cell_2_born_2, cell_2_surv_2, cell_3_born_2, cell_3_surv_2,
       cell_4_born_2, cell_4_surv_2, cell_5_born_2, cell_5_surv_2, cell_6_born_2, cell_6_surv_2,
       cell_7_born_2, cell_7_surv_2, cell_8_born_2, cell_8_surv_2, cell_9_born_2, cell_9_surv_2,
       cell_10_born_2, cell_10_surv_2, cell_11_born_2, cell_11_surv_2, cell_12_born_2, cell_12_surv_2,
       cell_13_born_2, cell_13_surv_2, cell_14_born_2, cell_14_surv_2, cell_15_born_2, cell_15_surv_2,
       cell_16_born_2, cell_16_surv_2, cell_17_born_2, cell_17_surv_2, cell_18_born_2, cell_18_surv_2,
       cell_19_born_2, cell_19_surv_2, cell_20_born_2, cell_20_surv_2, cell_21_born_2, cell_21_surv_2,
       cell_22_born_2, cell_22_surv_2, cell_23_born_2, cell_23_surv_2, cell_24_born_2, cell_24_surv_2,
       cell_25_born_2, cell_25_surv_2, cell_26_born_2, cell_26_surv_2, cell_27_born_2, cell_27_surv_2,
       cell_28_born_2, cell_28_surv_2, cell_29_born_2, cell_29_surv_2, cell_30_born_2, cell_30_surv_2,
       cell_31_born_2, cell_31_surv_2;

  and and_1 (and_1_out, \this [31], mode);
  and and_2 (and_2_out, above[31], mode);
  and and_3 (and_3_out, mode, below[31]);
  \cell  cell_1 (
    .surv(surv), .neighbor(and_1_out), .neighbor_2(cell_2_curr), .neighbor_3(and_3_out),
    .neighbor_4(below[1]), .self(\this [0]), .neighbor_5(above[1]), .neighbor_6(below[0]),
    .neighbor_7(above[0]), .neighbor_8(and_2_out), .born(born), .curr_2(cell_1_curr_2),
    .born_2(cell_1_born_2), .surv_2(cell_1_surv_2), .\new (out_7[0]));  // open: curr
  \cell  cell_2 (
    .surv(cell_1_surv_2), .neighbor(cell_1_curr_2), .neighbor_2(cell_3_curr), .neighbor_3(below[0]),
    .neighbor_4(below[2]), .self(\this [1]), .neighbor_5(above[2]), .neighbor_6(below[1]),
    .neighbor_7(above[1]), .neighbor_8(above[0]), .born(cell_1_born_2), .curr(cell_2_curr),
    .curr_2(cell_2_curr_2), .born_2(cell_2_born_2), .surv_2(cell_2_surv_2), .\new (out_7[1]));
  \cell  cell_3 (
    .surv(cell_2_surv_2), .neighbor(cell_2_curr_2), .neighbor_2(cell_4_curr), .neighbor_3(below[1]),
    .neighbor_4(below[3]), .self(\this [2]), .neighbor_5(above[3]), .neighbor_6(below[2]),
    .neighbor_7(above[2]), .neighbor_8(above[1]), .born(cell_2_born_2), .curr(cell_3_curr),
    .curr_2(cell_3_curr_2), .born_2(cell_3_born_2), .surv_2(cell_3_surv_2), .\new (out_7[2]));
  \cell  cell_4 (
    .surv(cell_3_surv_2), .neighbor(cell_3_curr_2), .neighbor_2(cell_5_curr), .neighbor_3(below[2]),
    .neighbor_4(below[4]), .self(\this [3]), .neighbor_5(above[4]), .neighbor_6(below[3]),
    .neighbor_7(above[3]), .neighbor_8(above[2]), .born(cell_3_born_2), .curr(cell_4_curr),
    .curr_2(cell_4_curr_2), .born_2(cell_4_born_2), .surv_2(cell_4_surv_2), .\new (out_7[3]));
  \cell  cell_5 (
    .surv(cell_4_surv_2), .neighbor(cell_4_curr_2), .neighbor_2(cell_6_curr), .neighbor_3(below[3]),
    .neighbor_4(below[5]), .self(\this [4]), .neighbor_5(above[5]), .neighbor_6(below[4]),
    .neighbor_7(above[4]), .neighbor_8(above[3]), .born(cell_4_born_2), .curr(cell_5_curr),
    .curr_2(cell_5_curr_2), .born_2(cell_5_born_2), .surv_2(cell_5_surv_2), .\new (out_7[4]));
  \cell  cell_6 (
    .surv(cell_5_surv_2), .neighbor(cell_5_curr_2), .neighbor_2(cell_7_curr), .neighbor_3(below[4]),
    .neighbor_4(below[6]), .self(\this [5]), .neighbor_5(above[6]), .neighbor_6(below[5]),
    .neighbor_7(above[5]), .neighbor_8(above[4]), .born(cell_5_born_2), .curr(cell_6_curr),
    .curr_2(cell_6_curr_2), .born_2(cell_6_born_2), .surv_2(cell_6_surv_2), .\new (out_7[5]));
  \cell  cell_7 (
    .surv(cell_6_surv_2), .neighbor(cell_6_curr_2), .neighbor_2(cell_8_curr), .neighbor_3(below[5]),
    .neighbor_4(below[7]), .self(\this [6]), .neighbor_5(above[7]), .neighbor_6(below[6]),
    .neighbor_7(above[6]), .neighbor_8(above[5]), .born(cell_6_born_2), .curr(cell_7_curr),
    .curr_2(cell_7_curr_2), .born_2(cell_7_born_2), .surv_2(cell_7_surv_2), .\new (out_7[6]));
  \cell  cell_8 (
    .surv(cell_7_surv_2), .neighbor(cell_7_curr_2), .neighbor_2(cell_9_curr), .neighbor_3(below[6]),
    .neighbor_4(below[8]), .self(\this [7]), .neighbor_5(above[8]), .neighbor_6(below[7]),
    .neighbor_7(above[7]), .neighbor_8(above[6]), .born(cell_7_born_2), .curr(cell_8_curr),
    .curr_2(cell_8_curr_2), .born_2(cell_8_born_2), .surv_2(cell_8_surv_2), .\new (out_7[7]));
  \cell  cell_9 (
    .surv(cell_8_surv_2), .neighbor(cell_8_curr_2), .neighbor_2(cell_10_curr), .neighbor_3(below[7]),
    .neighbor_4(below[9]), .self(\this [8]), .neighbor_5(above[9]), .neighbor_6(below[8]),
    .neighbor_7(above[8]), .neighbor_8(above[7]), .born(cell_8_born_2), .curr(cell_9_curr),
    .curr_2(cell_9_curr_2), .born_2(cell_9_born_2), .surv_2(cell_9_surv_2), .\new (out_7[8]));
  \cell  cell_10 (
    .surv(cell_9_surv_2), .neighbor(cell_9_curr_2), .neighbor_2(cell_11_curr), .neighbor_3(below[8]),
    .neighbor_4(below[10]), .self(\this [9]), .neighbor_5(above[10]), .neighbor_6(below[9]),
    .neighbor_7(above[9]), .neighbor_8(above[8]), .born(cell_9_born_2), .curr(cell_10_curr),
    .curr_2(cell_10_curr_2), .born_2(cell_10_born_2), .surv_2(cell_10_surv_2), .\new (out_7[9]));
  \cell  cell_11 (
    .surv(cell_10_surv_2), .neighbor(cell_10_curr_2), .neighbor_2(cell_12_curr), .neighbor_3(below[9]),
    .neighbor_4(below[11]), .self(\this [10]), .neighbor_5(above[11]), .neighbor_6(below[10]),
    .neighbor_7(above[10]), .neighbor_8(above[9]), .born(cell_10_born_2), .curr(cell_11_curr),
    .curr_2(cell_11_curr_2), .born_2(cell_11_born_2), .surv_2(cell_11_surv_2), .\new (out_7[10]));
  \cell  cell_12 (
    .surv(cell_11_surv_2), .neighbor(cell_11_curr_2), .neighbor_2(cell_13_curr), .neighbor_3(below[10]),
    .neighbor_4(below[12]), .self(\this [11]), .neighbor_5(above[12]), .neighbor_6(below[11]),
    .neighbor_7(above[11]), .neighbor_8(above[10]), .born(cell_11_born_2), .curr(cell_12_curr),
    .curr_2(cell_12_curr_2), .born_2(cell_12_born_2), .surv_2(cell_12_surv_2), .\new (out_7[11]));
  \cell  cell_13 (
    .surv(cell_12_surv_2), .neighbor(cell_12_curr_2), .neighbor_2(cell_14_curr), .neighbor_3(below[11]),
    .neighbor_4(below[13]), .self(\this [12]), .neighbor_5(above[13]), .neighbor_6(below[12]),
    .neighbor_7(above[12]), .neighbor_8(above[11]), .born(cell_12_born_2), .curr(cell_13_curr),
    .curr_2(cell_13_curr_2), .born_2(cell_13_born_2), .surv_2(cell_13_surv_2), .\new (out_7[12]));
  \cell  cell_14 (
    .surv(cell_13_surv_2), .neighbor(cell_13_curr_2), .neighbor_2(cell_15_curr), .neighbor_3(below[12]),
    .neighbor_4(below[14]), .self(\this [13]), .neighbor_5(above[14]), .neighbor_6(below[13]),
    .neighbor_7(above[13]), .neighbor_8(above[12]), .born(cell_13_born_2), .curr(cell_14_curr),
    .curr_2(cell_14_curr_2), .born_2(cell_14_born_2), .surv_2(cell_14_surv_2), .\new (out_7[13]));
  \cell  cell_15 (
    .surv(cell_14_surv_2), .neighbor(cell_14_curr_2), .neighbor_2(cell_16_curr), .neighbor_3(below[13]),
    .neighbor_4(below[15]), .self(\this [14]), .neighbor_5(above[15]), .neighbor_6(below[14]),
    .neighbor_7(above[14]), .neighbor_8(above[13]), .born(cell_14_born_2), .curr(cell_15_curr),
    .curr_2(cell_15_curr_2), .born_2(cell_15_born_2), .surv_2(cell_15_surv_2), .\new (out_7[14]));
  \cell  cell_16 (
    .surv(cell_15_surv_2), .neighbor(cell_15_curr_2), .neighbor_2(cell_17_curr), .neighbor_3(below[14]),
    .neighbor_4(below[16]), .self(\this [15]), .neighbor_5(above[16]), .neighbor_6(below[15]),
    .neighbor_7(above[15]), .neighbor_8(above[14]), .born(cell_15_born_2), .curr(cell_16_curr),
    .curr_2(cell_16_curr_2), .born_2(cell_16_born_2), .surv_2(cell_16_surv_2), .\new (out_7[15]));
  \cell  cell_17 (
    .surv(cell_16_surv_2), .neighbor(cell_16_curr_2), .neighbor_2(cell_18_curr), .neighbor_3(below[15]),
    .neighbor_4(below[17]), .self(\this [16]), .neighbor_5(above[17]), .neighbor_6(below[16]),
    .neighbor_7(above[16]), .neighbor_8(above[15]), .born(cell_16_born_2), .curr(cell_17_curr),
    .curr_2(cell_17_curr_2), .born_2(cell_17_born_2), .surv_2(cell_17_surv_2), .\new (out_7[16]));
  \cell  cell_18 (
    .surv(cell_17_surv_2), .neighbor(cell_17_curr_2), .neighbor_2(cell_19_curr), .neighbor_3(below[16]),
    .neighbor_4(below[18]), .self(\this [17]), .neighbor_5(above[18]), .neighbor_6(below[17]),
    .neighbor_7(above[17]), .neighbor_8(above[16]), .born(cell_17_born_2), .curr(cell_18_curr),
    .curr_2(cell_18_curr_2), .born_2(cell_18_born_2), .surv_2(cell_18_surv_2), .\new (out_7[17]));
  \cell  cell_19 (
    .surv(cell_18_surv_2), .neighbor(cell_18_curr_2), .neighbor_2(cell_20_curr), .neighbor_3(below[17]),
    .neighbor_4(below[19]), .self(\this [18]), .neighbor_5(above[19]), .neighbor_6(below[18]),
    .neighbor_7(above[18]), .neighbor_8(above[17]), .born(cell_18_born_2), .curr(cell_19_curr),
    .curr_2(cell_19_curr_2), .born_2(cell_19_born_2), .surv_2(cell_19_surv_2), .\new (out_7[18]));
  \cell  cell_20 (
    .surv(cell_19_surv_2), .neighbor(cell_19_curr_2), .neighbor_2(cell_21_curr), .neighbor_3(below[18]),
    .neighbor_4(below[20]), .self(\this [19]), .neighbor_5(above[20]), .neighbor_6(below[19]),
    .neighbor_7(above[19]), .neighbor_8(above[18]), .born(cell_19_born_2), .curr(cell_20_curr),
    .curr_2(cell_20_curr_2), .born_2(cell_20_born_2), .surv_2(cell_20_surv_2), .\new (out_7[19]));
  \cell  cell_21 (
    .surv(cell_20_surv_2), .neighbor(cell_20_curr_2), .neighbor_2(cell_22_curr), .neighbor_3(below[19]),
    .neighbor_4(below[21]), .self(\this [20]), .neighbor_5(above[21]), .neighbor_6(below[20]),
    .neighbor_7(above[20]), .neighbor_8(above[19]), .born(cell_20_born_2), .curr(cell_21_curr),
    .curr_2(cell_21_curr_2), .born_2(cell_21_born_2), .surv_2(cell_21_surv_2), .\new (out_7[20]));
  \cell  cell_22 (
    .surv(cell_21_surv_2), .neighbor(cell_21_curr_2), .neighbor_2(cell_23_curr), .neighbor_3(below[20]),
    .neighbor_4(below[22]), .self(\this [21]), .neighbor_5(above[22]), .neighbor_6(below[21]),
    .neighbor_7(above[21]), .neighbor_8(above[20]), .born(cell_21_born_2), .curr(cell_22_curr),
    .curr_2(cell_22_curr_2), .born_2(cell_22_born_2), .surv_2(cell_22_surv_2), .\new (out_7[21]));
  \cell  cell_23 (
    .surv(cell_22_surv_2), .neighbor(cell_22_curr_2), .neighbor_2(cell_24_curr), .neighbor_3(below[21]),
    .neighbor_4(below[23]), .self(\this [22]), .neighbor_5(above[23]), .neighbor_6(below[22]),
    .neighbor_7(above[22]), .neighbor_8(above[21]), .born(cell_22_born_2), .curr(cell_23_curr),
    .curr_2(cell_23_curr_2), .born_2(cell_23_born_2), .surv_2(cell_23_surv_2), .\new (out_7[22]));
  \cell  cell_24 (
    .surv(cell_23_surv_2), .neighbor(cell_23_curr_2), .neighbor_2(cell_25_curr), .neighbor_3(below[22]),
    .neighbor_4(below[24]), .self(\this [23]), .neighbor_5(above[24]), .neighbor_6(below[23]),
    .neighbor_7(above[23]), .neighbor_8(above[22]), .born(cell_23_born_2), .curr(cell_24_curr),
    .curr_2(cell_24_curr_2), .born_2(cell_24_born_2), .surv_2(cell_24_surv_2), .\new (out_7[23]));
  \cell  cell_25 (
    .surv(cell_24_surv_2), .neighbor(cell_24_curr_2), .neighbor_2(cell_26_curr), .neighbor_3(below[23]),
    .neighbor_4(below[25]), .self(\this [24]), .neighbor_5(above[25]), .neighbor_6(below[24]),
    .neighbor_7(above[24]), .neighbor_8(above[23]), .born(cell_24_born_2), .curr(cell_25_curr),
    .curr_2(cell_25_curr_2), .born_2(cell_25_born_2), .surv_2(cell_25_surv_2), .\new (out_7[24]));
  \cell  cell_26 (
    .surv(cell_25_surv_2), .neighbor(cell_25_curr_2), .neighbor_2(cell_27_curr), .neighbor_3(below[24]),
    .neighbor_4(below[26]), .self(\this [25]), .neighbor_5(above[26]), .neighbor_6(below[25]),
    .neighbor_7(above[25]), .neighbor_8(above[24]), .born(cell_25_born_2), .curr(cell_26_curr),
    .curr_2(cell_26_curr_2), .born_2(cell_26_born_2), .surv_2(cell_26_surv_2), .\new (out_7[25]));
  \cell  cell_27 (
    .surv(cell_26_surv_2), .neighbor(cell_26_curr_2), .neighbor_2(cell_28_curr), .neighbor_3(below[25]),
    .neighbor_4(below[27]), .self(\this [26]), .neighbor_5(above[27]), .neighbor_6(below[26]),
    .neighbor_7(above[26]), .neighbor_8(above[25]), .born(cell_26_born_2), .curr(cell_27_curr),
    .curr_2(cell_27_curr_2), .born_2(cell_27_born_2), .surv_2(cell_27_surv_2), .\new (out_7[26]));
  \cell  cell_28 (
    .surv(cell_27_surv_2), .neighbor(cell_27_curr_2), .neighbor_2(cell_29_curr), .neighbor_3(below[26]),
    .neighbor_4(below[28]), .self(\this [27]), .neighbor_5(above[28]), .neighbor_6(below[27]),
    .neighbor_7(above[27]), .neighbor_8(above[26]), .born(cell_27_born_2), .curr(cell_28_curr),
    .curr_2(cell_28_curr_2), .born_2(cell_28_born_2), .surv_2(cell_28_surv_2), .\new (out_7[27]));
  \cell  cell_29 (
    .surv(cell_28_surv_2), .neighbor(cell_28_curr_2), .neighbor_2(cell_30_curr), .neighbor_3(below[27]),
    .neighbor_4(below[29]), .self(\this [28]), .neighbor_5(above[29]), .neighbor_6(below[28]),
    .neighbor_7(above[28]), .neighbor_8(above[27]), .born(cell_28_born_2), .curr(cell_29_curr),
    .curr_2(cell_29_curr_2), .born_2(cell_29_born_2), .surv_2(cell_29_surv_2), .\new (out_7[28]));
  \cell  cell_30 (
    .surv(cell_29_surv_2), .neighbor(cell_29_curr_2), .neighbor_2(cell_31_curr), .neighbor_3(below[28]),
    .neighbor_4(below[30]), .self(\this [29]), .neighbor_5(above[30]), .neighbor_6(below[29]),
    .neighbor_7(above[29]), .neighbor_8(above[28]), .born(cell_29_born_2), .curr(cell_30_curr),
    .curr_2(cell_30_curr_2), .born_2(cell_30_born_2), .surv_2(cell_30_surv_2), .\new (out_7[29]));
  \cell  cell_31 (
    .surv(cell_30_surv_2), .neighbor(cell_30_curr_2), .neighbor_2(cell_32_curr), .neighbor_3(below[29]),
    .neighbor_4(below[31]), .self(\this [30]), .neighbor_5(above[31]), .neighbor_6(below[30]),
    .neighbor_7(above[30]), .neighbor_8(above[29]), .born(cell_30_born_2), .curr(cell_31_curr),
    .curr_2(cell_31_curr_2), .born_2(cell_31_born_2), .surv_2(cell_31_surv_2), .\new (out_7[30]));
  and and_4 (and_4_out, above[0], mode);
  \cell  cell_32 (
    .surv(cell_31_surv_2), .neighbor(cell_31_curr_2), .neighbor_2(and_6_out), .neighbor_3(below[30]),
    .neighbor_4(and_5_out), .self(\this [31]), .neighbor_5(and_4_out), .neighbor_6(below[31]),
    .neighbor_7(above[31]), .neighbor_8(above[30]), .born(cell_31_born_2), .curr(cell_32_curr),
    .\new (out_7[31]));  // open: curr_2, born_2, surv_2
  and and_5 (and_5_out, mode, below[0]);
  and and_6 (and_6_out, mode, \this [0]);

  // Other names for the same wires on the sheet: _31 = \this [31]
endmodule

module \cell  (
  input  [8:0] surv,
  input  neighbor,
  input  neighbor_2,
  input  neighbor_3,
  input  neighbor_4,
  input  self,
  input  neighbor_5,
  input  neighbor_6,
  input  neighbor_7,
  input  neighbor_8,
  input  [8:0] born,
  output [8:0] surv_2,
  output curr,
  output curr_2,
  output \new ,
  output [8:0] born_2
);

  wire multiplexer_1_out, multiplexer_2_out, or_1_out, or_2_out, or_3_out;
  wire [3:0] counter_1_out_9;

  counter counter_1 (
    .in_1(neighbor), .in_2(neighbor_2), .in_3(neighbor_3), .in_4(neighbor_4), .in_5(neighbor_5),
    .in_6(neighbor_6), .in_7(neighbor_7), .in_8(neighbor_8), .out_9(counter_1_out_9));
  Multiplexer #(.select(4), .enable("false")) multiplexer_1 (
    .in0(surv[0]), .in1(surv[1]), .in2(surv[2]), .in3(surv[3]), .in4(surv[4]), .in5(surv[5]), .in6(surv[6]),
    .in7(surv[7]), .in8(surv[8]), .out(multiplexer_1_out), .sel(counter_1_out_9));  // open: in9, in10, in11, in12, in13, in14, in15
  Multiplexer #(.select(4), .enable("false")) multiplexer_2 (
    .in0(born[0]), .in1(born[1]), .in2(born[2]), .in3(born[3]), .in4(born[4]), .in5(born[5]), .in6(born[6]),
    .in7(born[7]), .in8(born[8]), .out(multiplexer_2_out), .sel(counter_1_out_9));  // open: in9, in10, in11, in12, in13, in14, in15
  or or_1 (or_1_out, multiplexer_1_out, multiplexer_2_out, self);
  or or_2 (or_2_out, multiplexer_1_out, multiplexer_2_out, ~self);  // OR_Gate
  or or_3 (or_3_out, ~multiplexer_1_out, multiplexer_2_out, self);  // OR_Gate
  and and_1 (\new , or_1_out, or_2_out, or_3_out);

  assign born_2 = born;
  assign curr = self;
  assign curr_2 = self;
  assign surv_2 = surv;
endmodule

module counter (
  input  in_1,
  input  in_2,
  input  in_3,
  input  in_4,
  input  in_5,
  input  in_6,
  input  in_7,
  input  in_8,
  output [3:0] out_9
);

  wire [1:0] adder_1_out, adder_2_out, adder_3_out, adder_4_out, adder_5_out, adder_6_out;
  wire [2:2] adder_5_cout, adder_6_cout;

  Adder #(.width(1)) adder_1 (.a(in_1), .b(in_2), .out(adder_1_out[0]), .cout(adder_1_out[1]));  // open: cin
  Adder #(.width(1)) adder_2 (.a(in_3), .b(in_4), .out(adder_2_out[0]), .cout(adder_2_out[1]));  // open: cin
  Adder #(.width(1)) adder_3 (.a(in_5), .b(in_6), .out(adder_3_out[0]), .cout(adder_3_out[1]));  // open: cin
  Adder #(.width(1)) adder_4 (.a(in_7), .b(in_8), .out(adder_4_out[0]), .cout(adder_4_out[1]));  // open: cin
  Adder #(.width(2)) adder_5 (
    .a(adder_1_out), .b(adder_2_out), .out(adder_5_out), .cout(adder_5_cout[2]));  // open: cin
  Adder #(.width(2)) adder_6 (
    .a(adder_3_out), .b(adder_4_out), .out(adder_6_out), .cout(adder_6_cout[2]));  // open: cin
  Adder #(.width(3)) adder_7 (
    .a({adder_5_cout[2], adder_5_out}), .b({adder_6_cout[2], adder_6_out}), .out(out_9[2:0]), .cout(out_9[3]));  // open: cin
endmodule

module gameProcessor (
  input  mode,
  input  clock,
  input  play,
  input  [8:0] surv,
  input  [8:0] born,
  input  reset,
  input  [31:0] in_7,
  input  [31:0] in_8,
  input  [31:0] in_9,
  input  [31:0] in_10,
  input  [31:0] in_11,
  input  [31:0] in_12,
  input  [31:0] in_13,
  input  [31:0] in_14,
  input  [31:0] in_15,
  input  [31:0] in_16,
  input  [31:0] in_17,
  input  [31:0] in_18,
  input  [31:0] in_19,
  input  [31:0] in_20,
  input  [31:0] in_21,
  input  [31:0] in_22,
  input  [31:0] in_23,
  input  [31:0] in_24,
  input  [31:0] in_25,
  input  [31:0] in_26,
  input  [31:0] in_27,
  input  [31:0] in_28,
  input  [31:0] in_29,
  input  [31:0] in_30,
  input  [31:0] in_31,
  input  [31:0] in_32,
  input  [31:0] in_33,
  input  [31:0] in_34,
  input  [31:0] in_35,
  input  [31:0] in_36,
  input  [31:0] in_37,
  input  [31:0] in_38,
  output cc,
  output [31:0] out_40,
  output [31:0] out_41,
  output [31:0] out_42,
  output [31:0] out_43,
  output [31:0] out_44,
  output [31:0] out_45,
  output [31:0] out_46,
  output [31:0] out_47,
  output [31:0] out_48,
  output [31:0] out_49,
  output [31:0] out_50,
  output [31:0] out_51,
  output [31:0] out_52,
  output [31:0] out_53,
  output [31:0] out_54,
  output [31:0] out_55,
  output [31:0] out_56,
  output [31:0] out_57,
  output [31:0] out_58,
  output [31:0] out_59,
  output [31:0] out_60,
  output [31:0] out_61,
  output [31:0] out_62,
  output [31:0] out_63,
  output [31:0] out_64,
  output [31:0] out_65,
  output [31:0] out_66,
  output [31:0] out_67,
  output [31:0] out_68,
  output [31:0] out_69,
  output [31:0] out_70,
  output [31:0] out_71
);

  wire comparator_1_eq, nor_1_out, not_1_out, not_2_out, or_1_out;
  wire [4:0] cnt;
  wire [31:0] demultiplexer_1_out0, gameprocessorrow_1_out_7, multiplexer_1_out, multiplexer_2_out,
       multiplexer_3_out, multiplexer_4_out, multiplexer_5_out;

  not not_1 (not_1_out, comparator_1_eq);
  and and_1 (cc, not_1_out, comparator_1_eq);
  Comparator #(.width(5)) comparator_1 (.a({5{1'b0}}), .b(cnt), .eq(comparator_1_eq));  // open: gt, lt
  Counter #(.width(5), .max('h1f), .trigger("falling")) counter_1 (
    .count(play), .Q(cnt), .clk(clock), .clr(or_1_out));  // open: load, D, carry
  or or_1 (or_1_out, nor_1_out, reset);
  nor nor_1 (nor_1_out, play, not_2_out);
  not not_2 (not_2_out, play);
  Multiplexer #(.width(32), .enable("false")) multiplexer_1 (
    .in0({32{1'b0}}), .in1(in_38), .out(multiplexer_1_out), .sel(mode));
  Multiplexer #(.width(32), .enable("false")) multiplexer_2 (
    .in0({32{1'b0}}), .in1(in_7), .out(multiplexer_2_out), .sel(mode));
  Multiplexer #(.select(5), .width(32), .enable("false")) multiplexer_3 (
    .in0(multiplexer_1_out), .in1(in_7), .in2(in_8), .in3(in_9), .in4(in_10), .in5(in_11), .in6(in_12),
    .in7(in_13), .in8(in_14), .in9(in_15), .in10(in_16), .in11(in_17), .in12(in_18), .in13(in_19),
    .in14(in_20), .in15(in_21), .in16(in_22), .in17(in_23), .in18(in_24), .in19(in_25), .in20(in_26),
    .in21(in_27), .in22(in_28), .in23(in_29), .in24(in_30), .in25(in_31), .in26(in_32), .in27(in_33),
    .in28(in_34), .in29(in_35), .in30(in_36), .in31(in_37), .out(multiplexer_3_out), .sel(cnt));
  Multiplexer #(.select(5), .width(32), .enable("false")) multiplexer_4 (
    .in0(in_7), .in1(in_8), .in2(in_9), .in3(in_10), .in4(in_11), .in5(in_12), .in6(in_13), .in7(in_14),
    .in8(in_15), .in9(in_16), .in10(in_17), .in11(in_18), .in12(in_19), .in13(in_20), .in14(in_21),
    .in15(in_22), .in16(in_23), .in17(in_24), .in18(in_25), .in19(in_26), .in20(in_27), .in21(in_28),
    .in22(in_29), .in23(in_30), .in24(in_31), .in25(in_32), .in26(in_33), .in27(in_34), .in28(in_35),
    .in29(in_36), .in30(in_37), .in31(in_38), .out(multiplexer_4_out), .sel(cnt));
  Multiplexer #(.select(5), .width(32), .enable("false")) multiplexer_5 (
    .in0(in_8), .in1(in_9), .in2(in_10), .in3(in_11), .in4(in_12), .in5(in_13), .in6(in_14), .in7(in_15),
    .in8(in_16), .in9(in_17), .in10(in_18), .in11(in_19), .in12(in_20), .in13(in_21), .in14(in_22),
    .in15(in_23), .in16(in_24), .in17(in_25), .in18(in_26), .in19(in_27), .in20(in_28), .in21(in_29),
    .in22(in_30), .in23(in_31), .in24(in_32), .in25(in_33), .in26(in_34), .in27(in_35), .in28(in_36),
    .in29(in_37), .in30(in_38), .in31(multiplexer_2_out), .out(multiplexer_5_out), .sel(cnt));
  gameProcessorrow gameprocessorrow_1 (
    .\this (multiplexer_4_out), .out_7(gameprocessorrow_1_out_7), .surv(surv), .born(born),
    .below(multiplexer_3_out), .above(multiplexer_5_out), .mode(mode));
  Demultiplexer #(.select(5), .disabled(0)) demultiplexer_1 (
    .out0(demultiplexer_1_out0[0]), .out1(demultiplexer_1_out0[1]), .out2(demultiplexer_1_out0[2]),
    .out3(demultiplexer_1_out0[3]), .out4(demultiplexer_1_out0[4]), .out5(demultiplexer_1_out0[5]),
    .out6(demultiplexer_1_out0[6]), .out7(demultiplexer_1_out0[7]), .out8(demultiplexer_1_out0[8]),
    .out9(demultiplexer_1_out0[9]), .out10(demultiplexer_1_out0[10]), .out11(demultiplexer_1_out0[11]),
    .out12(demultiplexer_1_out0[12]), .out13(demultiplexer_1_out0[13]), .out14(demultiplexer_1_out0[14]),
    .out15(demultiplexer_1_out0[15]), .out16(demultiplexer_1_out0[16]), .out17(demultiplexer_1_out0[17]),
    .out18(demultiplexer_1_out0[18]), .out19(demultiplexer_1_out0[19]), .out20(demultiplexer_1_out0[20]),
    .out21(demultiplexer_1_out0[21]), .out22(demultiplexer_1_out0[22]), .out23(demultiplexer_1_out0[23]),
    .out24(demultiplexer_1_out0[24]), .out25(demultiplexer_1_out0[25]), .out26(demultiplexer_1_out0[26]),
    .out27(demultiplexer_1_out0[27]), .out28(demultiplexer_1_out0[28]), .out29(demultiplexer_1_out0[29]),
    .out30(demultiplexer_1_out0[30]), .out31(demultiplexer_1_out0[31]), .in(clock), .sel(cnt), .en(play));
  Register #(.width(32)) register_1 (
    .D(gameprocessorrow_1_out_7), .Q(out_40), .clk(demultiplexer_1_out0[0]));  // open: en, clr
  Register #(.width(32)) register_2 (
    .D(gameprocessorrow_1_out_7), .Q(out_41), .clk(demultiplexer_1_out0[1]));  // open: en, clr
  Register #(.width(32)) register_3 (
    .D(gameprocessorrow_1_out_7), .Q(out_42), .clk(demultiplexer_1_out0[2]));  // open: en, clr
  Register #(.width(32)) register_4 (
    .D(gameprocessorrow_1_out_7), .Q(out_43), .clk(demultiplexer_1_out0[3]));  // open: en, clr
  Register #(.width(32)) register_5 (
    .D(gameprocessorrow_1_out_7), .Q(out_44), .clk(demultiplexer_1_out0[4]));  // open: en, clr
  Register #(.width(32)) register_6 (
    .D(gameprocessorrow_1_out_7), .Q(out_45), .clk(demultiplexer_1_out0[5]));  // open: en, clr
  Register #(.width(32)) register_7 (
    .D(gameprocessorrow_1_out_7), .Q(out_46), .clk(demultiplexer_1_out0[6]));  // open: en, clr
  Register #(.width(32)) register_8 (
    .D(gameprocessorrow_1_out_7), .Q(out_47), .clk(demultiplexer_1_out0[7]));  // open: en, clr
  Register #(.width(32)) register_9 (
    .D(gameprocessorrow_1_out_7), .Q(out_48), .clk(demultiplexer_1_out0[8]));  // open: en, clr
  Register #(.width(32)) register_10 (
    .D(gameprocessorrow_1_out_7), .Q(out_49), .clk(demultiplexer_1_out0[9]));  // open: en, clr
  Register #(.width(32)) register_11 (
    .D(gameprocessorrow_1_out_7), .Q(out_50), .clk(demultiplexer_1_out0[10]));  // open: en, clr
  Register #(.width(32)) register_12 (
    .D(gameprocessorrow_1_out_7), .Q(out_51), .clk(demultiplexer_1_out0[11]));  // open: en, clr
  Register #(.width(32)) register_13 (
    .D(gameprocessorrow_1_out_7), .Q(out_52), .clk(demultiplexer_1_out0[12]));  // open: en, clr
  Register #(.width(32)) register_14 (
    .D(gameprocessorrow_1_out_7), .Q(out_53), .clk(demultiplexer_1_out0[13]));  // open: en, clr
  Register #(.width(32)) register_15 (
    .D(gameprocessorrow_1_out_7), .Q(out_54), .clk(demultiplexer_1_out0[14]));  // open: en, clr
  Register #(.width(32)) register_16 (
    .D(gameprocessorrow_1_out_7), .Q(out_55), .clk(demultiplexer_1_out0[15]));  // open: en, clr
  Register #(.width(32)) register_17 (
    .D(gameprocessorrow_1_out_7), .Q(out_56), .clk(demultiplexer_1_out0[16]));  // open: en, clr
  Register #(.width(32)) register_18 (
    .D(gameprocessorrow_1_out_7), .Q(out_57), .clk(demultiplexer_1_out0[17]));  // open: en, clr
  Register #(.width(32)) register_19 (
    .D(gameprocessorrow_1_out_7), .Q(out_58), .clk(demultiplexer_1_out0[18]));  // open: en, clr
  Register #(.width(32)) register_20 (
    .D(gameprocessorrow_1_out_7), .Q(out_59), .clk(demultiplexer_1_out0[19]));  // open: en, clr
  Register #(.width(32)) register_21 (
    .D(gameprocessorrow_1_out_7), .Q(out_60), .clk(demultiplexer_1_out0[20]));  // open: en, clr
  Register #(.width(32)) register_22 (
    .D(gameprocessorrow_1_out_7), .Q(out_61), .clk(demultiplexer_1_out0[21]));  // open: en, clr
  Register #(.width(32)) register_23 (
    .D(gameprocessorrow_1_out_7), .Q(out_62), .clk(demultiplexer_1_out0[22]));  // open: en, clr
  Register #(.width(32)) register_24 (
    .D(gameprocessorrow_1_out_7), .Q(out_63), .clk(demultiplexer_1_out0[23]));  // open: en, clr
  Register #(.width(32)) register_25 (
    .D(gameprocessorrow_1_out_7), .Q(out_64), .clk(demultiplexer_1_out0[24]));  // open: en, clr
  Register #(.width(32)) register_26 (
    .D(gameprocessorrow_1_out_7), .Q(out_65), .clk(demultiplexer_1_out0[25]));  // open: en, clr
  Register #(.width(32)) register_27 (
    .D(gameprocessorrow_1_out_7), .Q(out_66), .clk(demultiplexer_1_out0[26]));  // open: en, clr
  Register #(.width(32)) register_28 (
    .D(gameprocessorrow_1_out_7), .Q(out_67), .clk(demultiplexer_1_out0[27]));  // open: en, clr
  Register #(.width(32)) register_29 (
    .D(gameprocessorrow_1_out_7), .Q(out_68), .clk(demultiplexer_1_out0[28]));  // open: en, clr
  Register #(.width(32)) register_30 (
    .D(gameprocessorrow_1_out_7), .Q(out_69), .clk(demultiplexer_1_out0[29]));  // open: en, clr
  Register #(.width(32)) register_31 (
    .D(gameprocessorrow_1_out_7), .Q(out_70), .clk(demultiplexer_1_out0[30]));  // open: en, clr
  Register #(.width(32)) register_32 (
    .D(gameprocessorrow_1_out_7), .Q(out_71), .clk(demultiplexer_1_out0[31]));  // open: en, clr

  // Other names for the same wires on the sheet: wi0[31:0] = out_40; wi1[31:0] = out_41; wi2[31:0] = out_42;
  //   wi3[31:0] = out_43; wi4[31:0] = out_44; wi5[31:0] = out_45; wi6[31:0] = out_46; wi7[31:0] = out_47;
  //   wi8[31:0] = out_48; wi9[31:0] = out_49; wi10[31:0] = out_50; wi11[31:0] = out_51; wi12[31:0] = out_52;
  //   wi13[31:0] = out_53; wi14[31:0] = out_54; wi15[31:0] = out_55; wi16[31:0] = out_56; wi17[31:0] = out_57;
  //   wi18[31:0] = out_58; wi19[31:0] = out_59; wi20[31:0] = out_60; wi21[31:0] = out_61; wi22[31:0] = out_62;
  //   wi23[31:0] = out_63; wi24[31:0] = out_64; wi25[31:0] = out_65; wi26[31:0] = out_66; wi27[31:0] = out_67;
  //   wi28[31:0] = out_68; wi29[31:0] = out_69; wi30[31:0] = out_70; wi31[31:0] = out_71; wo0[31:0] = in_7;
  //   wo1[31:0] = in_8; wo2[31:0] = in_9; wo3[31:0] = in_10; wo4[31:0] = in_11; wo5[31:0] = in_12; wo6[31:0] = in_13;
  //   wo7[31:0] = in_14; wo8[31:0] = in_15; wo9[31:0] = in_16; wo10[31:0] = in_17; wo11[31:0] = in_18;
  //   wo12[31:0] = in_19; wo13[31:0] = in_20; wo14[31:0] = in_21; wo15[31:0] = in_22; wo16[31:0] = in_23;
  //   wo17[31:0] = in_24; wo18[31:0] = in_25; wo19[31:0] = in_26; wo20[31:0] = in_27; wo21[31:0] = in_28;
  //   wo22[31:0] = in_29; wo23[31:0] = in_30; wo24[31:0] = in_31; wo25[31:0] = in_32; wo26[31:0] = in_33;
  //   wo27[31:0] = in_34; wo28[31:0] = in_35; wo29[31:0] = in_36; wo30[31:0] = in_37; wo31[31:0] = in_38

  // Notes on the sheet:
  //   0 - bounds
  //   1 - toroidal
endmodule

module speedController (
  input  [1:0] speed,
  input  play,
  input  clock,
  output modClock
);

  wire and_1_out, and_2_out, and_3_out, counter_1_carry, counter_2_carry, counter_3_carry,
       demultiplexer_1_out0, demultiplexer_1_out1, demultiplexer_1_out2, demultiplexer_1_out3, nor_1_out,
       not_1_out, not_2_out, not_3_out, not_4_out;

  Demultiplexer #(.select(2)) demultiplexer_1 (
    .out0(demultiplexer_1_out0), .out1(demultiplexer_1_out1), .out2(demultiplexer_1_out2),
    .out3(demultiplexer_1_out3), .in(clock), .sel(speed), .en(play));
  Counter #(.width(1), .max('h1)) counter_1 (
    .carry(counter_1_carry), .clk(demultiplexer_1_out1), .clr(nor_1_out));  // open: load, D, count, Q
  Counter #(.width(2), .max('h3)) counter_2 (
    .carry(counter_2_carry), .clk(demultiplexer_1_out2), .clr(nor_1_out));  // open: load, D, count, Q
  Counter #(.width(3), .max('h7)) counter_3 (
    .carry(counter_3_carry), .clk(demultiplexer_1_out3), .clr(nor_1_out));  // open: load, D, count, Q
  nor nor_1 (nor_1_out, play, not_4_out);
  not not_1 (not_1_out, counter_1_carry);
  not not_2 (not_2_out, counter_2_carry);
  not not_3 (not_3_out, counter_3_carry);
  not not_4 (not_4_out, play);
  and and_1 (and_1_out, not_1_out, counter_1_carry);
  and and_2 (and_2_out, not_2_out, counter_2_carry);
  and and_3 (and_3_out, not_3_out, counter_3_carry);
  Multiplexer #(.select(2), .enable("false")) multiplexer_1 (
    .in0(demultiplexer_1_out0), .in1(and_1_out), .in2(and_2_out), .in3(and_3_out), .out(modClock), .sel(speed));
endmodule
