// Logisim project UART_Controller.circ as structural Verilog: 2 circuits, main circuit uart
module uart (
  input  clock,
  input  I_Osel,
  input  rd_wr,
  input  [15:0] data,
  input  [7:0] I_Oaddr
);

  wire and_1_out, and_2_out, and_4_out, uart_1_p1, uart_1_p7, uart_1_p8;
  wire [7:0] uart_1_p2, uart_1_p3;

  Pull_Resistor pull_resistor_1 (.node(data[14]));
  Pull_Resistor pull_resistor_2 (.node(data[15]));
  Pull_Resistor pull_resistor_3 (.node(data[12]));
  Pull_Resistor pull_resistor_4 (.node(data[13]));
  Pull_Resistor pull_resistor_5 (.node(data[8]));
  Pull_Resistor pull_resistor_6 (.node(data[9]));
  Pull_Resistor pull_resistor_7 (.node(data[10]));
  Pull_Resistor pull_resistor_8 (.node(data[11]));
  assign data[7:0] = and_1_out ? uart_1_p2 : 8'bz;  // Controlled_Buffer controlled_buffer_1
  and and_1 (and_1_out, rd_wr, uart_1_p8);
  // UART uart_1: pin names not known; wires that end beside it: uart_1_p1, uart_1_p2, uart_1_p3, uart_1_p1, clock, rd_wr, uart_1_p7, uart_1_p8
  and and_2 (and_2_out, ~rd_wr, uart_1_p8);  // AND_Gate
  assign uart_1_p3 = and_2_out ? data[7:0] : 8'bz;  // Controlled_Buffer controlled_buffer_2
  LED led_1 (.in(uart_1_p7));
  and and_3 (uart_1_p8, and_4_out, I_Osel);
  and and_4 (and_4_out, ~I_Oaddr[7], I_Oaddr[6], I_Oaddr[5], I_Oaddr[4], I_Oaddr[3], I_Oaddr[2], ~I_Oaddr[1], ~I_Oaddr[0]);  // AND_Gate

  // Notes on the sheet:
  //   To interrupt arbiter
endmodule

module IntArb (
  input  clock,
  input  IAck,
  input  dp,
  input  con,
  output IRQ,
  output [5:0] vec
);

  wire and_1_out, and_2_out, and_3_out, nor_1_out, not_1_out, not_2_out, not_3_out, or_1_out, or_2_out,
       or_3_out, or_4_out;
  wire [5:0] and_4_out, and_5_out, and_6_out, or_5_out;
  wire [5:5] Connection_q, DataAvail_q, DataEnd_q;

  not not_1 (not_1_out, dp);
  and and_1 (and_1_out, not_1_out, dp);
  not not_2 (not_2_out, dp);
  nor nor_1 (nor_1_out, not_2_out, dp);
  not not_3 (not_3_out, con);
  and and_2 (and_2_out, not_3_out, con);
  assign vec = and_3_out ? or_5_out : 6'bz;  // Controlled_Buffer controlled_buffer_1
  and and_3 (and_3_out, IRQ, IAck);
  or or_1 (or_1_out, and_2_out, nor_1_out);
  or or_2 (or_2_out, and_1_out, nor_1_out);
  or or_3 (or_3_out, and_1_out, and_2_out);
  or or_4 (or_4_out, and_2_out, nor_1_out, and_1_out);
  S_R_Flip_Flop #(.trigger("high")) DataAvail (
    .S(and_1_out), .clk(1'b1), .R(or_1_out), .Q(DataAvail_q[5]));  // open: Qn, preset, reset, en
  S_R_Flip_Flop #(.trigger("high")) Connection (
    .S(and_2_out), .clk(1'b1), .R(or_2_out), .Q(Connection_q[5]));  // open: Qn, preset, reset, en
  S_R_Flip_Flop #(.trigger("high")) DataEnd (
    .S(nor_1_out), .clk(1'b1), .R(or_3_out), .Q(DataEnd_q[5]));  // open: Qn, preset, reset, en
  assign and_4_out = {6{DataAvail_q[5]}} & {6{1'b0}};  // AND_Gate and_4, 6 bits wide
  assign and_5_out = {6{Connection_q[5]}} & 6'b000001;  // AND_Gate and_5, 6 bits wide
  assign and_6_out = {6{DataEnd_q[5]}} & 6'b000010;  // AND_Gate and_6, 6 bits wide
  assign or_5_out = and_4_out | and_5_out | and_6_out;  // OR_Gate or_5, 6 bits wide
  S_R_Flip_Flop #(.trigger("falling")) s_r_ff_1 (
    .S(1'b0), .clk(clock), .R(IAck), .Q(IRQ), .preset(or_4_out));  // open: Qn, reset, en
endmodule
