// Logisim project arbiter.circ as structural Verilog: 1 circuit, main circuit main
module main (
  input  IRQ,
  input  IAck,
  input  [5:0] dvec,
  input  DIRQ,
  output IRQ_2,
  output [5:0] vecbus,
  output IACk_2,
  output DIAck
);

  wire and_1_out, and_2_out, and_3_out, and_4_out, counter_1_q, decoder_1_out0, decoder_1_out1, nor_1_out,
       nor_2_out, not_1_out, not_2_out, not_3_out, not_4_out, or_1_out, s_r_ff_1_q, s_r_ff_2_qn, to0_out,
       to1_out;

  Decoder #(.enable("false")) decoder_1 (.out0(decoder_1_out0), .out1(decoder_1_out1), .sel(counter_1_q));
  Counter #(.width(1), .max('h1)) counter_1 (.Q(counter_1_q), .clk(or_1_out));  // open: load, D, count, carry, clr
  assign DIAck = decoder_1_out1 ? IAck : 1'bz;  // Controlled_Buffer controlled_buffer_1
  Pull_Resistor pull_resistor_1 (.node(DIAck));
  or or_1 (or_1_out, to0_out, to1_out);
  S_R_Flip_Flop s_r_ff_1 (.Q(s_r_ff_1_q), .preset(and_1_out), .reset(not_1_out));  // open: S, clk, R, Qn, en
  not not_1 (not_1_out, DIAck);
  and and_1 (and_1_out, decoder_1_out1, DIAck);
  and and_2 (and_2_out, IRQ, decoder_1_out0);
  or or_2 (IRQ_2, and_2_out, and_3_out);
  and and_3 (and_3_out, decoder_1_out1, DIRQ);
  assign vecbus = s_r_ff_1_q ? dvec : 6'bz;  // Controlled_Buffer controlled_buffer_2
  and to0 (to0_out, decoder_1_out1, nor_1_out);
  not not_2 (not_2_out, IAck);
  nor nor_1 (nor_1_out, not_2_out, IAck);
  and to1 (to1_out, decoder_1_out0, s_r_ff_2_qn, DIRQ);
  S_R_Flip_Flop s_r_ff_2 (.Q(IACk_2), .Qn(s_r_ff_2_qn), .preset(and_4_out), .reset(nor_2_out));  // open: S, clk, R, en
  and and_4 (and_4_out, ~DIRQ, IAck, not_3_out);  // AND_Gate
  nor nor_2 (nor_2_out, IAck, not_4_out);
  not not_3 (not_3_out, IAck);
  not not_4 (not_4_out, IAck);

  // Notes on the sheet:
  //   1 - int in progress
  //   0 - idle/wait another irq to end
endmodule
