// Logisim project main.circ as structural Verilog: 1 circuit, main circuit main
module main (
);

  wire and_1_out, and_2_out, and_3_out, and_4_out, and_5_out, and_6_out, and_8_out, and_11_out, cdm_16_1_p1,
       cdm_16_1_p2, cdm_16_1_p4, cdm_16_1_p5, cdm_16_1_p6, cdm_16_1_p7, clock, controlled_buffer_9_out,
       controlled_buffer_12_out, HS, I_Osel, in_out_prime, mem, not_1_out, not_2_out, not_3_out, or_1_out,
       or_2_out, RAM, uart_1_p2, uart_1_p7, uart_1_p9, uart_1_p10, uart_1_p12, word;
  wire [3:0] controlled_buffer_7_out, controlled_buffer_11_out, controlled_buffer_13_out;
  wire [5:0] controlled_buffer_5_out;
  wire [7:0] uart_1_p3, uart_1_p4, uart_1_p11;
  wire [15:0] adr, cdm_16_1_p12, cdm_16_1_p13, controlled_buffer_3_out, controlled_buffer_6_out,
       controlled_buffer_8_out, controlled_buffer_14_out, data, main_1_dataout, status_q;
  wire [31:0] main_1_out_12, main_1_out_13, main_1_out_14, main_1_out_15, main_1_out_16, main_1_out_17,
       main_1_out_18, main_1_out_19, main_1_out_20, main_1_out_21, main_1_out_22, main_1_out_23,
       main_1_out_24, main_1_out_25, main_1_out_26, main_1_out_27, main_1_out_28, main_1_out_29,
       main_1_out_30, main_1_out_31, main_1_out_32, main_1_out_33, main_1_out_34, main_1_out_35,
       main_1_out_36, main_1_out_37, main_1_out_38, main_1_out_39, main_1_out_40, main_1_out_41,
       main_1_out_42, main_1_out_43;

  // Probe on cdm_16_1_p1
  // Probe on cdm_16_1_p2
  // CdM_16 cdm_16_1: pin names not known; wires that end beside it: cdm_16_1_p1, cdm_16_1_p2, clock, cdm_16_1_p4, cdm_16_1_p5, cdm_16_1_p6, cdm_16_1_p7, mem, in_out_prime, word, adr, cdm_16_1_p12, cdm_16_1_p13
  Clock clock_1 (.out(clock));
  Button Hard_reset (.out(HS));
  // Probe on cdm_16_1_p5
  // Probe on cdm_16_1_p4
  // Probe on cdm_16_1_p6
  // Probe on cdm_16_1_p7
  // Probe on adr
  assign data = not_1_out ? cdm_16_1_p12 : 16'bz;  // Controlled_Buffer controlled_buffer_1
  not not_1 (not_1_out, in_out_prime);
  assign cdm_16_1_p13 = in_out_prime ? data : 16'bz;  // Controlled_Buffer controlled_buffer_2
  and and_1 (and_1_out, ~adr[7], adr[6], adr[5], adr[4], adr[3], adr[2], adr[1], ~adr[0]);  // AND_Gate
  and and_2 (and_2_out, I_Osel, and_1_out);
  and and_3 (and_3_out, ~in_out_prime, and_2_out);  // AND_Gate
  assign controlled_buffer_3_out = and_3_out ? data : 16'bz;  // Controlled_Buffer controlled_buffer_3
  // RAM ram_1: pin names not known; wires that end beside it: adr, word, RAM, clock, in_out_prime, data
  assign data = and_4_out ? status_q : 16'bz;  // Controlled_Buffer controlled_buffer_4
  and and_4 (and_4_out, in_out_prime, and_2_out);
  Register #(.width(16)) status (.D(controlled_buffer_3_out), .en(and_2_out), .Q(status_q), .clk(clock), .clr(HS));
  // Probe on data
  and and_5 (and_5_out, adr[8], adr[9], adr[10], adr[11], adr[12], adr[13], adr[14], adr[15]);
  and and_6 (and_6_out, in_out_prime, and_2_out, data[13]);
  and and_7 (RAM, ~and_5_out, mem);  // AND_Gate
  and and_8 (and_8_out, I_Osel, adr[7]);
  and and_9 (I_Osel, mem, and_5_out);
  assign controlled_buffer_5_out = and_8_out ? adr[6:1] : 6'bz;  // Controlled_Buffer controlled_buffer_5
  not not_2 (not_2_out, in_out_prime);
  assign controlled_buffer_6_out = not_2_out ? data : 16'bz;  // Controlled_Buffer controlled_buffer_6
  assign controlled_buffer_7_out = status_q[12] ? status_q[3:0] : 4'bz;  // Controlled_Buffer controlled_buffer_7
  assign controlled_buffer_8_out = and_8_out ? controlled_buffer_6_out : 16'bz;  // Controlled_Buffer controlled_buffer_8
  assign controlled_buffer_9_out = and_8_out ? in_out_prime : 1'bz;  // Controlled_Buffer controlled_buffer_9
  or or_1 (or_1_out, status_q[12], and_8_out);
  assign data = in_out_prime ? main_1_dataout : 16'bz;  // Controlled_Buffer controlled_buffer_10
  assign controlled_buffer_11_out = status_q[12] ? status_q[11:8] : 4'bz;  // Controlled_Buffer controlled_buffer_11
  assign controlled_buffer_12_out = or_1_out ? clock : 1'bz;  // Controlled_Buffer controlled_buffer_12
  Matrix_Controller_main main_1 (
    .sel(and_8_out), .play(status_q[12]), .reset(or_2_out), .out_12(main_1_out_12), .out_13(main_1_out_13),
    .out_14(main_1_out_14), .out_15(main_1_out_15), .out_16(main_1_out_16), .out_17(main_1_out_17),
    .out_18(main_1_out_18), .out_19(main_1_out_19), .out_20(main_1_out_20), .out_21(main_1_out_21),
    .out_22(main_1_out_22), .out_23(main_1_out_23), .out_24(main_1_out_24), .out_25(main_1_out_25),
    .out_26(main_1_out_26), .out_27(main_1_out_27), .out_28(main_1_out_28), .clock(controlled_buffer_12_out),
    .out_29(main_1_out_29), .out_30(main_1_out_30), .out_31(main_1_out_31), .out_32(main_1_out_32),
    .out_33(main_1_out_33), .out_34(main_1_out_34), .out_35(main_1_out_35), .out_42(main_1_out_42),
    .out_43(main_1_out_43), .addr(controlled_buffer_5_out), .die1(controlled_buffer_7_out),
    .die2(controlled_buffer_13_out), .respawn(controlled_buffer_11_out), .out_36(main_1_out_36),
    .out_37(main_1_out_37), .out_38(main_1_out_38), .out_39(main_1_out_39), .out_40(main_1_out_40),
    .out_41(main_1_out_41), .datain(controlled_buffer_8_out), .dataout(main_1_dataout),
    .rd_wr_prime(controlled_buffer_9_out));
  DotMatrix #(.inputtype("row"), .matrixcols(32), .matrixrows(32)) dotmatrix_1 (
    .row0(main_1_out_12), .row1(main_1_out_13), .row2(main_1_out_14), .row3(main_1_out_15),
    .row4(main_1_out_16), .row5(main_1_out_17), .row6(main_1_out_18), .row7(main_1_out_19),
    .row8(main_1_out_20), .row9(main_1_out_21), .row10(main_1_out_22), .row11(main_1_out_23),
    .row12(main_1_out_24), .row13(main_1_out_25), .row14(main_1_out_26), .row15(main_1_out_27),
    .row16(main_1_out_28), .row17(main_1_out_29), .row18(main_1_out_30), .row19(main_1_out_31),
    .row20(main_1_out_32), .row21(main_1_out_33), .row22(main_1_out_34), .row23(main_1_out_35),
    .row24(main_1_out_36), .row25(main_1_out_37), .row26(main_1_out_38), .row27(main_1_out_39),
    .row28(main_1_out_40), .row29(main_1_out_41), .row30(main_1_out_42), .row31(main_1_out_43));
  assign controlled_buffer_13_out = status_q[12] ? status_q[7:4] : 4'bz;  // Controlled_Buffer controlled_buffer_13
  or or_2 (or_2_out, and_6_out, HS);
  Pull_Resistor pull_resistor_1 (.node(controlled_buffer_14_out[13]));
  Pull_Resistor pull_resistor_2 (.node(controlled_buffer_14_out[14]));
  Pull_Resistor pull_resistor_3 (.node(controlled_buffer_14_out[11]));
  Pull_Resistor pull_resistor_4 (.node(controlled_buffer_14_out[15]));
  Pull_Resistor pull_resistor_5 (.node(controlled_buffer_14_out[12]));
  Pull_Resistor pull_resistor_6 (.node(controlled_buffer_14_out[10]));
  Pull_Resistor pull_resistor_7 (.node(controlled_buffer_14_out[8]));
  Pull_Resistor pull_resistor_8 (.node(controlled_buffer_14_out[9]));
  assign controlled_buffer_14_out[7:0] = not_3_out ? uart_1_p3 : 8'bz;  // Controlled_Buffer controlled_buffer_14
  // UART uart_1: pin names not known; wires that end beside it: controlled_buffer_14_out, uart_1_p2, uart_1_p3, uart_1_p4, uart_1_p2, clock, uart_1_p7, uart_1_p7, uart_1_p9, uart_1_p10, uart_1_p11, uart_1_p12
  not not_3 (not_3_out, uart_1_p7);
  assign uart_1_p4 = uart_1_p7 ? controlled_buffer_14_out[7:0] : 8'bz;  // Controlled_Buffer controlled_buffer_15
  LED led_1 (.in(uart_1_p9));
  and and_10 (uart_1_p10, and_11_out, uart_1_p12);
  and and_11 (and_11_out, ~uart_1_p11[7], uart_1_p11[6], uart_1_p11[5], uart_1_p11[4], uart_1_p11[3], uart_1_p11[2], ~uart_1_p11[1], ~uart_1_p11[0]);  // AND_Gate

  // Other names for the same wires on the sheet: I_Oaddr[7:0] = adr[7:0]; I_Odat[15:0] = data;
  //   rd_wr_prime = in_out_prime

  // Notes on the sheet:
  //   To interrupt arbiter
endmodule
